// Logisim project teamwork.circ as structural Verilog: 17 circuits, main circuit 游戏面板
module \游戏面板  (
);

  wire and_1_out, and_2_out, CLK, CLK_t, comparator_1_eq, comparator_1_lt, gameover_1_gameover, not_1_out,
       or_1_out, RST, Score, START, \减速 , \加速 , \键盘操作电路_1_left_a , \键盘操作电路_1_right_d ;
  wire [3:0] \HP个位 , \HP十位 , \HP百位 ;
  wire [6:0] keyboard_1_data;
  wire [7:0] counter_1_q;
  wire [15:0] \速度 , \速度初始 ;
  wire [31:0] \点阵显示_1__1 , \点阵显示_1__2 , \点阵显示_1__3 , \点阵显示_1__4 , \点阵显示_1__5 , \点阵显示_1__6 , \点阵显示_1__7 ,
       \点阵显示_1__8 , \点阵显示_1__9 , \点阵显示_1__10 , \点阵显示_1__11 , \点阵显示_1__12 , \点阵显示_1__13 , \点阵显示_1__14 ,
       \点阵显示_1__15 , \点阵显示_1__16 , \点阵显示_1__17 , \点阵显示_1__18 , \点阵显示_1__19 , \点阵显示_1__20 , \点阵显示_1__21 ,
       \点阵显示_1__22 , \点阵显示_1__23 , \点阵显示_1__24 , \点阵显示_1__25 , \点阵显示_1__26 , \点阵显示_1__27 , \点阵显示_1__28 ,
       \点阵显示_1__29 , \点阵显示_1__30 , \点阵显示_1__31 , \点阵显示_1__32 ;

  DotMatrix #(.inputtype("column"), .matrixcols(9), .matrixrows(9), .persist(0), .dotshape("square")) dotmatrix_1 (
    .col0({9{1'b0}}), .col1(9'h78), .col2(9'hfc), .col3(9'hfe), .col4(9'h7f), .col5(9'hfe), .col6(9'hfc),
    .col7(9'h78), .col8({9{1'b0}}));
  Hex_Digit_Display hex_digit_display_1 (.value(\HP百位 ));  // open: dp
  Hex_Digit_Display hex_digit_display_2 (.value(\HP个位 ));  // open: dp
  Hex_Digit_Display hex_digit_display_3 (.value(\HP十位 ));  // open: dp
  Counter #(.width(8), .max('hff), .ongoal("wrap"), .trigger("rising"), .behavior("old")) counter_1 (
    .count(1'b1), .Q(counter_1_q), .clk(Score), .clr(RST));  // open: load, D, carry, preset
  Button button_1 (.out(START));
  Button button_2 (.out(RST));
  GameOver gameover_1 (
    .delHP(counter_1_q), .exHP(8'h3), .Gameover(gameover_1_gameover), .\百位 (\HP百位 ), .\十位 (\HP十位 ),
    .\个位 (\HP个位 ));
  Clock #(.highDuration(1), .lowDuration(1)) clock_1 (.out(CLK));
  DotMatrix #(.inputtype("column"), .matrixcols(32), .matrixrows(32), .persist(0), .dotshape("square")) dotmatrix_2 (
    .col0(\点阵显示_1__1 ), .col1(\点阵显示_1__2 ), .col2(\点阵显示_1__3 ), .col3(\点阵显示_1__4 ), .col4(\点阵显示_1__5 ),
    .col5(\点阵显示_1__6 ), .col6(\点阵显示_1__7 ), .col7(\点阵显示_1__8 ), .col8(\点阵显示_1__9 ), .col9(\点阵显示_1__10 ),
    .col10(\点阵显示_1__11 ), .col11(\点阵显示_1__12 ), .col12(\点阵显示_1__13 ), .col13(\点阵显示_1__14 ),
    .col14(\点阵显示_1__15 ), .col15(\点阵显示_1__16 ), .col16(\点阵显示_1__17 ), .col17(\点阵显示_1__18 ),
    .col18(\点阵显示_1__19 ), .col19(\点阵显示_1__20 ), .col20(\点阵显示_1__21 ), .col21(\点阵显示_1__22 ),
    .col22(\点阵显示_1__23 ), .col23(\点阵显示_1__24 ), .col24(\点阵显示_1__25 ), .col25(\点阵显示_1__26 ),
    .col26(\点阵显示_1__27 ), .col27(\点阵显示_1__28 ), .col28(\点阵显示_1__29 ), .col29(\点阵显示_1__30 ),
    .col30(\点阵显示_1__31 ), .col31(\点阵显示_1__32 ));
  \点阵显示  \u_点阵显示_1  (
    .\结束 (gameover_1_gameover), .\开始 (START), .CLK(and_1_out), .RST(RST), .\上 (\键盘操作电路_1_left_a ),
    .\下 (\键盘操作电路_1_right_d ), ._1(\点阵显示_1__1 ), ._2(\点阵显示_1__2 ), ._3(\点阵显示_1__3 ), ._4(\点阵显示_1__4 ),
    ._5(\点阵显示_1__5 ), ._6(\点阵显示_1__6 ), ._7(\点阵显示_1__7 ), ._8(\点阵显示_1__8 ), ._9(\点阵显示_1__9 ),
    ._10(\点阵显示_1__10 ), ._11(\点阵显示_1__11 ), ._12(\点阵显示_1__12 ), ._13(\点阵显示_1__13 ), ._14(\点阵显示_1__14 ),
    ._15(\点阵显示_1__15 ), ._16(\点阵显示_1__16 ), ._17(\点阵显示_1__17 ), ._18(\点阵显示_1__18 ), ._19(\点阵显示_1__19 ),
    ._20(\点阵显示_1__20 ), ._21(\点阵显示_1__21 ), ._22(\点阵显示_1__22 ), ._23(\点阵显示_1__23 ), ._24(\点阵显示_1__24 ),
    ._25(\点阵显示_1__25 ), ._26(\点阵显示_1__26 ), ._27(\点阵显示_1__27 ), ._28(\点阵显示_1__28 ), ._29(\点阵显示_1__29 ),
    ._30(\点阵显示_1__30 ), .\得分 (Score), ._31(\点阵显示_1__31 ), ._32(\点阵显示_1__32 ));
  buf and_1 (and_1_out, not_1_out);  // AND_Gate
  not not_1 (not_1_out, CLK_t);
  Button button_3 (.out(\加速 ));
  Button button_4 (.out(\减速 ));
  \键盘操作电路  \u_键盘操作电路_1  (
    .\键盘输入 (keyboard_1_data), .CLK(CLK_t), .RST(RST), .LEFT_A(\键盘操作电路_1_left_a ), .RIGHT_D(\键盘操作电路_1_right_d ));
  Keyboard #(.Char_bit_width(7), .buflen(32), .trigger("rising")) keyboard_1 (
    .clk(CLK_t), .data(keyboard_1_data));  // open: re, clr, avail
  Comparator #(.width(16), .mode("twosComplement")) comparator_1 (
    .a(\速度初始 ), .b(16'h1), .eq(comparator_1_eq), .lt(comparator_1_lt));  // open: gt
  Multiplexer #(.select(1), .width(16), .disabled("Z"), .enable("false")) multiplexer_1 (
    .in0(\速度初始 ), .in1(16'h1), .out(\速度 ), .sel(comparator_1_lt));
  and and_2 (and_2_out, ~comparator_1_eq, \加速 );  // AND_Gate
  Counter #(.width(16), .max('hffff), .ongoal("wrap"), .trigger("rising"), .behavior("new")) counter_2 (
    .load(comparator_1_lt), .D(16'h1), .Q(\速度初始 ), .clk(or_1_out), .down(and_2_out));  // open: count, carry, clr, preset
  or or_1 (or_1_out, and_2_out, \减速 );

  // Notes on the sheet:
  //   HP
endmodule

module \玩家移动  (
  input  IR1,
  input  IR2,
  input  IR3,
  input  RST,
  input  CLK,
  output [31:0] \行1 ,
  output [31:0] \行2 ,
  output [31:0] \行3 ,
  output [31:0] \行4 ,
  output [31:0] \行5 ,
  output [31:0] \行6 ,
  output [31:0] \行7 ,
  output [31:0] \行8 ,
  output [31:0] \行9 ,
  output [31:0] \行10 ,
  output [31:0] \行11 ,
  output [31:0] \行12 ,
  output [31:0] \行13 ,
  output [31:0] \行14 ,
  output [31:0] \行15 ,
  output [31:0] \行16 ,
  output [31:0] \行17 ,
  output [31:0] \行18 ,
  output [31:0] \行19 ,
  output [31:0] \行20 ,
  output [31:0] \行21 ,
  output [31:0] \行22 ,
  output [31:0] \行23 ,
  output [31:0] \行24 ,
  output [31:0] \行25 ,
  output [31:0] \行26 ,
  output [31:0] \行27 ,
  output [31:0] \行28 ,
  output [31:0] \行29 ,
  output [31:0] \行30 ,
  output [31:0] \行31 ,
  output [31:0] \行32 
);

  wire ALUeq, ALUge, ALUle, and_1_out, and_2_out, and_3_out, and_5_out, and_6_out, and_7_out, and_8_out,
       and_9_out, and_10_out, Beq, Bne, Btype, clock_1_out, CLR1, CLR2, CLR3, comparator_1_eq,
       comparator_2_eq, comparator_3_eq, comparator_4_eq, comparator_5_eq, comparator_5_lt, comparator_6_eq,
       comparator_6_gt, comparator_6_lt, comparator_7_lt, comparator_8_eq, d_ff_1_q, d_ff_2_q, d_ff_3_q,
       d_ff_5_q, ecall, Go, halt, IE, INTR, INTR1, INTR2, INTR3, IR1_t, IR2_t, IR3_t, IRA, IRB, IRC, IRHAVE,
       JAL, JALR, Jtype, MemToReg, MemWrite, nand_1_out, not_1_out, not_2_out, not_3_out, or_1_out, or_2_out,
       or_7_out, or_9_out, or_13_out, or_14_out, or_16_out, or_17_out, RegWrite, Stype, URET, W1, W2, W3,
       \单周期硬布线控制器_1_alu_src ;
  wire [1:0] priority_encoder_1_out, priority_encoder_2_out, priority_encoder_3_out, register_2_q;
  wire [3:0] \单周期硬布线控制器_1_alu_op ;
  wire [4:0] multiplexer_4_out, multiplexer_5_out;
  wire [9:0] Addr;
  wire [12:0] CNT_num;
  wire [15:0] \总周期数 ;
  wire [31:0] a1, ALUres, bit_extender_1_out, bit_extender_2_out, bit_extender_3_out, bit_extender_4_out,
       Dout, IR, IR_PC, LedData, \mapreg_1_1_行1 , \mapreg_1_1_行2 , \mapreg_1_1_行3 , \mapreg_1_1_行4 ,
       \mapreg_1_1_行5 , \mapreg_1_1_行6 , \mapreg_1_1_行7 , \mapreg_1_1_行8 , \mapreg_1_1_行9 , \mapreg_1_1_行10 ,
       \mapreg_1_1_行11 , \mapreg_1_1_行12 , \mapreg_1_1_行13 , \mapreg_1_1_行14 , \mapreg_1_1_行15 ,
       \mapreg_1_1_行16 , \mapreg_1_1_行17 , \mapreg_1_1_行18 , \mapreg_1_1_行19 , \mapreg_1_1_行20 ,
       \mapreg_1_1_行21 , \mapreg_1_1_行22 , \mapreg_1_1_行23 , \mapreg_1_1_行24 , \mapreg_1_1_行25 ,
       \mapreg_1_1_行26 , \mapreg_1_1_行27 , \mapreg_1_1_行28 , \mapreg_1_1_行29 , \mapreg_1_1_行30 ,
       \mapreg_1_1_行31 , \mapreg_1_1_行32 , MEPC, multiplexer_1_out, multiplexer_3_out, multiplexer_6_out,
       multiplexer_7_out, PC, PC_4, PC_B, PC_J, RDin, regifile_1_r1, shifter_1_out, shifter_2_out;

  Button \u_继续运行  (.out(Go));
  Button _1 (.out(IRA));
  Button _2 (.out(IRB));
  Button _3 (.out(IRC));
  LED #(.active("true")) led_1 (.in(W1));
  LED #(.active("true")) led_2 (.in(W2));
  LED #(.active("true")) led_3 (.in(W3));
  Hex_Digit_Display hex_digit_display_1 (.value(LedData[31:28]));  // open: dp
  Hex_Digit_Display hex_digit_display_2 (.value(LedData[27:24]));  // open: dp
  or or_1 (or_1_out, Go, not_1_out);
  not not_1 (not_1_out, halt);
  Hex_Digit_Display hex_digit_display_3 (.value(LedData[19:16]));  // open: dp
  Hex_Digit_Display hex_digit_display_4 (.value(LedData[23:20]));  // open: dp
  Counter #(.width(16), .max('hffff), .ongoal("wrap"), .trigger("rising"), .behavior("new")) counter_1 (
    .count(or_1_out), .Q(\总周期数 ), .clk(CLK));  // open: load, D, carry, clr, preset, down
  Comparator #(.width(16), .mode("twosComplement")) comparator_1 (
    .a(16'h23b), .b(\总周期数 ), .eq(comparator_1_eq));  // open: gt, lt
  Comparator #(.width(16), .mode("twosComplement")) comparator_2 (
    .a(\总周期数 ), .b(16'h1), .eq(comparator_2_eq));  // open: gt, lt
  Comparator #(.width(16), .mode("twosComplement")) comparator_3 (
    .a(\总周期数 ), .b(16'h4), .eq(comparator_3_eq));  // open: gt, lt
  Comparator #(.width(16), .mode("twosComplement")) comparator_4 (
    .a(\总周期数 ), .b(16'h7), .eq(comparator_4_eq));  // open: gt, lt
  Hex_Digit_Display hex_digit_display_5 (.value(LedData[15:12]));  // open: dp
  Hex_Digit_Display hex_digit_display_6 (.value(LedData[11:8]));  // open: dp
  or or_2 (or_2_out, comparator_1_eq, comparator_2_eq);
  assign IRA = or_2_out ? ~CLK : 1'bz;  // Controlled_Inverter controlled_inverter_1
  assign IRB = comparator_3_eq ? ~CLK : 1'bz;  // Controlled_Inverter controlled_inverter_2
  assign IRC = comparator_4_eq ? ~CLK : 1'bz;  // Controlled_Inverter controlled_inverter_3
  Hex_Digit_Display hex_digit_display_7 (.value(LedData[3:0]));  // open: dp
  Hex_Digit_Display hex_digit_display_8 (.value(LedData[7:4]));  // open: dp
  // Probe on \总周期数 
  Pull_Resistor #(.pull(0)) pull_resistor_1 (.node(IRA));
  Pull_Resistor #(.pull(0)) pull_resistor_2 (.node(IRB));
  Pull_Resistor #(.pull(0)) pull_resistor_3 (.node(IRC));
  Priority_Encoder #(.select(2), .disabled("Z")) priority_encoder_1 (
    .in0(INTR1), .in1(INTR2), .in2(INTR3), .out(priority_encoder_1_out));  // open: in3, gs, en_out, en_in
  Priority_Encoder #(.select(2), .disabled("Z")) priority_encoder_2 (
    .in0(1'b1), .in1(JALR), .in2(JAL), .in3(Btype), .out(priority_encoder_2_out));  // open: gs, en_out, en_in
  Multiplexer #(.select(2), .width(32), .disabled("Z"), .enable("false")) multiplexer_1 (
    .in0(PC_4), .in1({ALUres[31:12], Addr, ALUres[1:0]}), .in2(PC_J), .in3(PC_B), .out(multiplexer_1_out),
    .sel(priority_encoder_2_out));
  Multiplexer #(.select(2), .width(32), .disabled("Z"), .enable("false")) multiplexer_2 (
    .in0(32'h30ac), .in1(32'h3150), .in2(32'h31f4), .out(IR_PC), .sel(priority_encoder_1_out));  // open: in3
  or or_3 (IR1_t, IR1, IRA);
  and and_1 (and_1_out, Beq, ALUeq);
  not not_2 (not_2_out, ALUeq);
  and and_2 (and_2_out, not_2_out, Bne);
  Priority_Encoder #(.select(2), .disabled("Z")) priority_encoder_3 (
    .in0(1'b1), .in1(INTR), .in2(URET), .out(priority_encoder_3_out));  // open: in3, gs, en_out, en_in
  or or_4 (W1, INTR1, d_ff_1_q);
  or or_5 (IR2_t, IR2, IRB);
  Register #(.width(32), .trigger("rising"), .Select("low")) register_1 (
    .D(multiplexer_1_out), .en(INTR), .Q(MEPC), .clk(CLK));  // open: clr
  Multiplexer #(.select(2), .width(32), .disabled("Z"), .enable("false")) multiplexer_3 (
    .in0(multiplexer_1_out), .in1(IR_PC), .in2(MEPC), .out(multiplexer_3_out), .sel(priority_encoder_3_out));  // open: in3
  D_Flip_Flop #(.trigger("rising"), .Pre_Clr_Positions("LEGACY"), .NegatePresetClear("false"), .enable("true"), .NewFFLayout("false")) d_ff_1 (
    .clk(IRA), .D(1'b1), .Q(d_ff_1_q), .reset(INTR1));  // open: Qn, preset, en
  Register #(.width(2), .trigger("rising"), .Select("low")) register_2 (
    .D(priority_encoder_1_out), .en(INTR), .Q(register_2_q), .clk(CLK));  // open: clr
  or or_6 (Btype, and_1_out, and_2_out);
  or or_7 (or_7_out, Go, not_3_out);
  not not_3 (not_3_out, halt);
  or or_8 (IRHAVE, INTR1, INTR2, INTR3);
  or or_9 (or_9_out, d_ff_1_q, INTR1);
  Demultiplexer #(.select(2), .width(1), .tristate("false"), .disabled("Z"), .enable("false")) demultiplexer_1 (
    .out0(CLR1), .out1(CLR2), .out2(CLR3), .in(URET), .sel(register_2_q));  // open: out3
  or or_10 (IR3_t, IR3, IRC);
  Register #(.width(32), .trigger("rising"), .Select("low")) u_PC (
    .D(multiplexer_3_out), .en(or_7_out), .Q(PC), .clk(CLK), .clr(RST));
  and and_3 (and_3_out, or_9_out, ~CLR1);  // AND_Gate
  or or_11 (Jtype, JAL, JALR);
  and and_4 (INTR, IE, IRHAVE);
  D_Flip_Flop #(.trigger("rising"), .Pre_Clr_Positions("LEGACY"), .NegatePresetClear("false"), .enable("true"), .NewFFLayout("false")) u_IR1 (
    .clk(CLK), .D(and_3_out), .Q(INTR1));  // open: Qn, preset, en, reset
  // RiscV_Probe riscv_probe_1: pin names not known; wires that end beside it: IR
  Adder #(.width(32)) adder_1 (.a(PC), .b(32'h4), .out(PC_4));  // open: cin, cout
  ROM #(.addrWidth(10), .dataWidth(32), .Select("high")) rom_1 (.addr(PC[11:2]), .data(IR));
  or or_12 (W2, INTR2, d_ff_2_q);
  \单周期硬布线控制器  \u_单周期硬布线控制器_1  (
    .OP(IR[6:2]), .Funct({IR[30], IR[25], IR[14:12]}), .ALU_OP(\单周期硬布线控制器_1_alu_op ), .in_3(IR[21]),
    .uret(URET), .MemToReg(MemToReg), .ecall(ecall), .MemWrite(MemWrite), .ALU_SRC(\单周期硬布线控制器_1_alu_src ),
    .RegWrite(RegWrite), .S_type(Stype), .Beq(Beq), .Bne(Bne), .Jalr(JALR), .JAL(JAL));  // open: CSRRCI, CSRRSI
  Multiplexer #(.select(1), .width(5), .disabled("Z"), .enable("false")) multiplexer_4 (
    .in0(IR[19:15]), .in1(5'b10001), .out(multiplexer_4_out), .sel(ecall));
  Multiplexer #(.select(1), .width(5), .disabled("Z"), .enable("false")) multiplexer_5 (
    .in0(IR[24:20]), .in1(5'b01010), .out(multiplexer_5_out), .sel(ecall));
  assign bit_extender_1_out = {{20{IR[31]}}, IR[31:20]};  // Bit_Extender bit_extender_1
  assign bit_extender_2_out = {{20{IR[31]}}, {IR[31:25], IR[11:7]}};  // Bit_Extender bit_extender_2
  D_Flip_Flop #(.trigger("rising"), .Pre_Clr_Positions("LEGACY"), .NegatePresetClear("false"), .enable("true"), .NewFFLayout("false")) d_ff_2 (
    .clk(IRB), .D(1'b1), .Q(d_ff_2_q), .reset(INTR2));  // open: Qn, preset, en
  Multiplexer #(.select(1), .width(32), .disabled("Z"), .enable("false")) multiplexer_6 (
    .in0(bit_extender_1_out), .in1(bit_extender_2_out), .out(multiplexer_6_out), .sel(Stype));
  assign bit_extender_3_out = {{20{IR[31]}}, {IR[31], IR[7], IR[30:25], IR[11:8]}};  // Bit_Extender bit_extender_3
  assign bit_extender_4_out = {{12{IR[31]}}, {IR[31], IR[19:12], IR[20], IR[30:21]}};  // Bit_Extender bit_extender_4
  or or_13 (or_13_out, d_ff_2_q, INTR2);
  D_Flip_Flop #(.trigger("high"), .Pre_Clr_Positions("LEGACY"), .NegatePresetClear("false"), .enable("true"), .NewFFLayout("false")) d_ff_3 (.Q(d_ff_3_q));  // open: clk, D, Qn, preset, en, reset
  // Probe on 13'hc
  Regifile regifile_1 (
    .Din(RDin), .Clk(CLK), .R1(regifile_1_r1), .R2(a1), .WE(RegWrite), .W_num(IR[11:7]),
    .R1_num(multiplexer_4_out), .R2_num(multiplexer_5_out));
  Shifter #(.width(32), .shift("ll")) shifter_1 (.in(bit_extender_3_out), .\dist (5'b00001), .out(shifter_1_out));
  Shifter #(.width(32), .shift("ll")) shifter_2 (.in(bit_extender_4_out), .\dist (5'b00001), .out(shifter_2_out));
  and and_5 (and_5_out, or_13_out, ~CLR2);  // AND_Gate
  Comparator #(.width(13), .mode("twosComplement")) comparator_5 (
    .a(CNT_num), .b(13'hc), .eq(comparator_5_eq), .lt(comparator_5_lt));  // open: gt
  Clock #(.highDuration(1), .lowDuration(1)) clock_1 (.out(clock_1_out));
  Multiplexer #(.select(1), .width(32), .disabled("Z"), .enable("false")) multiplexer_7 (
    .in0(a1), .in1(multiplexer_6_out), .out(multiplexer_7_out), .sel(\单周期硬布线控制器_1_alu_src ));
  Adder #(.width(32)) adder_2 (.a(shifter_1_out), .b(PC), .out(PC_B));  // open: cin, cout
  Adder #(.width(32)) adder_3 (.a(shifter_2_out), .b(PC), .out(PC_J));  // open: cin, cout
  D_Flip_Flop #(.trigger("rising"), .Pre_Clr_Positions("LEGACY"), .NegatePresetClear("false"), .enable("true"), .NewFFLayout("false")) u_IR2 (
    .clk(CLK), .D(and_5_out), .Q(INTR2));  // open: Qn, preset, en, reset
  nand nand_1 (nand_1_out, d_ff_3_q, comparator_5_eq);
  Counter #(.width(13), .max('h1fff), .ongoal("stay"), .trigger("rising"), .behavior("old")) counter_2 (
    .count(comparator_5_lt), .Q(CNT_num), .clk(clock_1_out));  // open: load, D, carry, clr, preset
  ALU alu_1 (
    .X(regifile_1_r1), .Y(multiplexer_7_out), .AluOP(\单周期硬布线控制器_1_alu_op ), .Equal(ALUeq),
    .Result({ALUres[31:12], Addr, ALUres[1:0]}), .out_4(ALUge), .out_6(ALUle));  // open: Result_2
  assign CLK = nand_1_out ? clock_1_out : 1'bz;  // Controlled_Buffer controlled_buffer_1
  Comparator #(.width(32), .mode("twosComplement")) comparator_6 (
    .a(32'h22), .b(regifile_1_r1), .gt(comparator_6_gt), .eq(comparator_6_eq), .lt(comparator_6_lt));
  or or_14 (or_14_out, ~IRHAVE, URET);  // OR_Gate
  Pull_Resistor #(.pull(1)) pull_resistor_4 (.node(CLK));
  Register #(.width(32), .trigger("rising"), .Select("low")) register_3 (
    .D(a1), .en(and_6_out), .Q(LedData), .clk(CLK));  // open: clr
  and and_6 (and_6_out, ecall, comparator_6_eq);
  or or_15 (W3, INTR3, d_ff_5_q);
  and and_7 (and_7_out, or_16_out, ecall);
  or or_16 (or_16_out, comparator_6_gt, comparator_6_lt);
  D_Flip_Flop #(.trigger("rising"), .Pre_Clr_Positions("LEGACY"), .NegatePresetClear("false"), .enable("true"), .NewFFLayout("true")) d_ff_4 (
    .clk(CLK), .D(or_14_out), .Q(IE));  // open: Qn, preset, en, reset
  D_Flip_Flop #(.trigger("rising"), .Pre_Clr_Positions("LEGACY"), .NegatePresetClear("false"), .enable("true"), .NewFFLayout("false")) d_ff_5 (
    .clk(IRC), .D(1'b1), .Q(d_ff_5_q), .reset(INTR3));  // open: Qn, preset, en
  RAM #(.addrWidth(10), .dataWidth(32), .bus("separate"), .Select("high")) ram_1 (
    .addr(Addr), .din(a1), .data(Dout), .str(MemWrite), .sel(1'b1), .clk(CLK), .ld(1'b1));  // open: clr
  Multiplexer #(.select(2), .width(32), .disabled("Z"), .enable("false")) multiplexer_8 (
    .in0({ALUres[31:12], Addr, ALUres[1:0]}), .in1(Dout), .in2(PC_4), .in3(PC_4), .out(RDin),
    .sel({Jtype, MemToReg}));
  or or_17 (or_17_out, d_ff_5_q, INTR3);
  D_Flip_Flop #(.trigger("falling"), .Pre_Clr_Positions("ABOVE_BELOW"), .NegatePresetClear("false"), .enable("true"), .NewFFLayout("true")) d_ff_6 (
    .clk(CLK), .D(1'b1), .Q(halt), .en(and_7_out), .reset(Go));  // open: Qn, preset
  and and_8 (and_8_out, or_17_out, ~CLR3);  // AND_Gate
  D_Flip_Flop #(.trigger("rising"), .Pre_Clr_Positions("LEGACY"), .NegatePresetClear("false"), .enable("true"), .NewFFLayout("false")) u_IR3 (
    .clk(CLK), .D(and_8_out), .Q(INTR3));  // open: Qn, preset, en, reset
  Comparator #(.width(10), .mode("twosComplement")) comparator_7 (
    .a(Addr), .b(10'h24), .lt(comparator_7_lt));  // open: gt, eq
  and and_9 (and_9_out, MemWrite, comparator_7_lt);
  Comparator #(.width(32), .mode("twosComplement")) comparator_8 (
    .a(a1), .b(32'hb), .eq(comparator_8_eq));  // open: gt, lt
  MapReg_1 mapreg_1_1 (
    .En(and_9_out), .Addr(Addr), .CLK(CLK), .Data(a1), .\行1 (\mapreg_1_1_行1 ), .\行9 (\mapreg_1_1_行9 ),
    .\行17 (\mapreg_1_1_行17 ), .\行25 (\mapreg_1_1_行25 ), .\行2 (\mapreg_1_1_行2 ), .\行10 (\mapreg_1_1_行10 ),
    .\行18 (\mapreg_1_1_行18 ), .\行26 (\mapreg_1_1_行26 ), .\行3 (\mapreg_1_1_行3 ), .\行11 (\mapreg_1_1_行11 ),
    .\行19 (\mapreg_1_1_行19 ), .\行27 (\mapreg_1_1_行27 ), .\行4 (\mapreg_1_1_行4 ), .\行12 (\mapreg_1_1_行12 ),
    .\行20 (\mapreg_1_1_行20 ), .\行28 (\mapreg_1_1_行28 ), .\行5 (\mapreg_1_1_行5 ), .\行13 (\mapreg_1_1_行13 ),
    .\行21 (\mapreg_1_1_行21 ), .\行29 (\mapreg_1_1_行29 ), .\行6 (\mapreg_1_1_行6 ), .\行14 (\mapreg_1_1_行14 ),
    .\行22 (\mapreg_1_1_行22 ), .\行30 (\mapreg_1_1_行30 ), .\行7 (\mapreg_1_1_行7 ), .\行15 (\mapreg_1_1_行15 ),
    .\行23 (\mapreg_1_1_行23 ), .\行31 (\mapreg_1_1_行31 ), .\行8 (\mapreg_1_1_行8 ), .\行16 (\mapreg_1_1_行16 ),
    .\行24 (\mapreg_1_1_行24 ), .\行32 (\mapreg_1_1_行32 ), .RST(RST));
  and and_10 (and_10_out, comparator_8_eq, ecall);
  MapReg_2 mapreg_2_1 (
    .En(and_10_out), ._1(\mapreg_1_1_行1 ), ._9(\mapreg_1_1_行9 ), ._17(\mapreg_1_1_行17 ),
    ._25(\mapreg_1_1_行25 ), ._2(\mapreg_1_1_行2 ), ._10(\mapreg_1_1_行10 ), ._18(\mapreg_1_1_行18 ),
    ._26(\mapreg_1_1_行26 ), ._3(\mapreg_1_1_行3 ), ._11(\mapreg_1_1_行11 ), ._19(\mapreg_1_1_行19 ),
    ._27(\mapreg_1_1_行27 ), ._4(\mapreg_1_1_行4 ), ._12(\mapreg_1_1_行12 ), ._20(\mapreg_1_1_行20 ),
    ._28(\mapreg_1_1_行28 ), ._5(\mapreg_1_1_行5 ), ._13(\mapreg_1_1_行13 ), ._21(\mapreg_1_1_行21 ),
    ._29(\mapreg_1_1_行29 ), ._6(\mapreg_1_1_行6 ), ._14(\mapreg_1_1_行14 ), ._22(\mapreg_1_1_行22 ),
    ._30(\mapreg_1_1_行30 ), ._7(\mapreg_1_1_行7 ), ._15(\mapreg_1_1_行15 ), ._23(\mapreg_1_1_行23 ),
    ._31(\mapreg_1_1_行31 ), ._8(\mapreg_1_1_行8 ), ._16(\mapreg_1_1_行16 ), ._24(\mapreg_1_1_行24 ),
    ._32(\mapreg_1_1_行32 ), .CLK(CLK), .\行1 (\行1 ), .\行9 (\行2 ), .\行17 (\行3 ), .\行25 (\行4 ), .\行2 (\行5 ),
    .\行10 (\行6 ), .\行18 (\行7 ), .\行26 (\行8 ), .\行3 (\行9 ), .\行11 (\行10 ), .\行19 (\行11 ), .\行27 (\行12 ),
    .\行4 (\行13 ), .\行12 (\行14 ), .\行20 (\行15 ), .\行28 (\行16 ), .\行5 (\行17 ), .\行13 (\行18 ), .\行21 (\行19 ),
    .\行29 (\行20 ), .\行6 (\行21 ), .\行14 (\行22 ), .\行22 (\行23 ), .\行30 (\行24 ), .\行7 (\行25 ), .\行15 (\行26 ),
    .\行23 (\行27 ), .\行31 (\行28 ), .\行8 (\行29 ), .\行16 (\行30 ), .\行24 (\行31 ), .\行32 (\行32 ), .RST(RST));

  // Other names for the same wires on the sheet: ALUres[11:2] = Addr; MDin[31:0] = a1

  // Notes on the sheet:
  //   中断源
  //   中断等待指示
  //   总复位信号应将除ROM以外所有存储组件全部清零
  //   单级中断测试信号模拟器
  //   数码管输出
  //   数码管输出应该用寄存器锁存，否则显示数据只能一闪而过
  //   RAM写使能MemWrite、RAM写入数据MDin等信号
  //   为方便自动评测，需要输出PC，IR，寄存器堆写如数据RDin
  //   中断响应阶段
  //   指令探针
  //   指令存储器
  //   中断响应
  //   指令字
  //   contents of rom_1 (hex, n*v repeats v):
  //   7d000113 100413 1f41993 41f9d993 433 c00913 800b13 140413 f47413 800293 100313 499993 89e9b3 1300533
  //   2200893 73 406282b3 fe0294e3 140413 f00f93 1f47433 1c41413 800293 100313 49d993 89e9b3 1300533
  //   2200893 73 406282b3 fe0294e3 1c45413 406b0b33 b0463 f95ff06f 2b3 fff2c293 1029293 fff2e293 500533
  //   2200893 73 f5dff06f 1112023 410113 a12023 410113 812023 410113 1312023 410113 1412023 410113 1512023
  //   410113 1612023 410113 100b13 300a13 100a93 1600433 441413 14469b3 1300533 2200893 73 fe0416e3
  //   415a0a33 fe0a10e3 ffc10113 12b03 ffc10113 12a83 ffc10113 12a03 ffc10113 12983 ffc10113 12403
  //   ffc10113 12503 ffc10113 12883 200073 1112023 410113 a12023 410113 812023 410113 1312023 410113
  //   1412023 410113 1512023 410113 1612023 410113 200b13 300a13 100a93 1600433 441413 14469b3 1300533
  //   2200893 73 fe0416e3 415a0a33 fe0a10e3 ffc10113 12b03 ffc10113 12a83 ffc10113 12a03 ffc10113 12983
  //   ffc10113 12403 ffc10113 12503 ffc10113 12883 200073 1112023 410113 a12023 410113 812023 410113
  //   1312023 410113 1412023 410113 1512023 410113 1612023 410113 300b13 300a13 100a93 1600433 441413
  //   14469b3 1300533 2200893 73 fe0416e3 415a0a33 fe0a10e3 ffc10113 12b03 ffc10113 12a83 ffc10113 12a03
  //   ffc10113 12983 ffc10113 12403 ffc10113 12503 ffc10113 12883 200073
  //   URET
  //   Beq
  //   Bne
  //   MemToReg
  //   MemWrite
  //   AluOP
  //   AluSrcB
  //   RegWrite
  //   控制位
  //   暂停节拍，不能为0
  //   戳工具置1进入计数暂停模式，ctrl+k时钟自动运行到对应节拍暂停
  //   ctrl+k关闭时钟连续运行，将控制位置零，进入单步调试模式调试
  //   中断使能位(用于开关中断)
  //   可计数暂停的时钟源
  //   数据存储器
  //   判断中断使能
endmodule

module \障碍下落  (
  input  IR1,
  input  IR2,
  input  IR3,
  input  RST,
  input  CLK,
  output [31:0] \行1 ,
  output [31:0] \行2 ,
  output [31:0] \行3 ,
  output [31:0] \行4 ,
  output [31:0] \行5 ,
  output [31:0] \行6 ,
  output [31:0] \行7 ,
  output [31:0] \行8 ,
  output [31:0] \行9 ,
  output [31:0] \行10 ,
  output [31:0] \行11 ,
  output [31:0] \行12 ,
  output [31:0] \行13 ,
  output [31:0] \行14 ,
  output [31:0] \行15 ,
  output [31:0] \行16 ,
  output [31:0] \行17 ,
  output [31:0] \行18 ,
  output [31:0] \行19 ,
  output [31:0] \行20 ,
  output [31:0] \行21 ,
  output [31:0] \行22 ,
  output [31:0] \行23 ,
  output [31:0] \行24 ,
  output [31:0] \行25 ,
  output [31:0] \行26 ,
  output [31:0] \行27 ,
  output [31:0] \行28 ,
  output [31:0] \行29 ,
  output [31:0] \行30 ,
  output [31:0] \行31 ,
  output [31:0] \行32 
);

  wire ALUeq, ALUge, ALUle, and_1_out, and_2_out, and_3_out, and_5_out, and_6_out, and_7_out, and_8_out,
       and_9_out, and_10_out, Beq, Bne, Btype, clock_1_out, CLR1, CLR2, CLR3, comparator_1_eq,
       comparator_2_eq, comparator_3_eq, comparator_4_eq, comparator_5_eq, comparator_5_lt, comparator_6_eq,
       comparator_6_gt, comparator_6_lt, comparator_7_lt, comparator_8_eq, d_ff_1_q, d_ff_2_q, d_ff_3_q,
       d_ff_5_q, ecall, Go, halt, IE, INTR, INTR1, INTR2, INTR3, IR1_t, IR2_t, IR3_t, IRA, IRB, IRC, IRHAVE,
       JAL, JALR, Jtype, MemToReg, MemWrite, nand_1_out, not_1_out, not_2_out, not_3_out, or_1_out, or_2_out,
       or_7_out, or_9_out, or_13_out, or_14_out, or_16_out, or_17_out, RegWrite, Stype, URET, W1, W2, W3,
       \单周期硬布线控制器_1_alu_src ;
  wire [1:0] priority_encoder_1_out, priority_encoder_2_out, priority_encoder_3_out, register_2_q;
  wire [3:0] \单周期硬布线控制器_1_alu_op ;
  wire [4:0] multiplexer_4_out, multiplexer_5_out;
  wire [9:0] Addr;
  wire [12:0] CNT_num;
  wire [15:0] \总周期数 ;
  wire [31:0] a1, ALUres, bit_extender_1_out, bit_extender_2_out, bit_extender_3_out, bit_extender_4_out,
       Dout, IR, IR_PC, LedData, \mapreg_1_1_行1 , \mapreg_1_1_行2 , \mapreg_1_1_行3 , \mapreg_1_1_行4 ,
       \mapreg_1_1_行5 , \mapreg_1_1_行6 , \mapreg_1_1_行7 , \mapreg_1_1_行8 , \mapreg_1_1_行9 , \mapreg_1_1_行10 ,
       \mapreg_1_1_行11 , \mapreg_1_1_行12 , \mapreg_1_1_行13 , \mapreg_1_1_行14 , \mapreg_1_1_行15 ,
       \mapreg_1_1_行16 , \mapreg_1_1_行17 , \mapreg_1_1_行18 , \mapreg_1_1_行19 , \mapreg_1_1_行20 ,
       \mapreg_1_1_行21 , \mapreg_1_1_行22 , \mapreg_1_1_行23 , \mapreg_1_1_行24 , \mapreg_1_1_行25 ,
       \mapreg_1_1_行26 , \mapreg_1_1_行27 , \mapreg_1_1_行28 , \mapreg_1_1_行29 , \mapreg_1_1_行30 ,
       \mapreg_1_1_行31 , \mapreg_1_1_行32 , MEPC, multiplexer_1_out, multiplexer_3_out, multiplexer_6_out,
       multiplexer_7_out, PC, PC_4, PC_B, PC_J, RDin, regifile_1_r1, shifter_1_out, shifter_2_out;

  Button \u_继续运行  (.out(Go));
  Button _1 (.out(IRA));
  Button _2 (.out(IRB));
  Button _3 (.out(IRC));
  LED #(.active("true")) led_1 (.in(W1));
  LED #(.active("true")) led_2 (.in(W2));
  LED #(.active("true")) led_3 (.in(W3));
  Hex_Digit_Display hex_digit_display_1 (.value(LedData[27:24]));  // open: dp
  Hex_Digit_Display hex_digit_display_2 (.value(LedData[31:28]));  // open: dp
  or or_1 (or_1_out, Go, not_1_out);
  not not_1 (not_1_out, halt);
  Hex_Digit_Display hex_digit_display_3 (.value(LedData[23:20]));  // open: dp
  Hex_Digit_Display hex_digit_display_4 (.value(LedData[19:16]));  // open: dp
  Counter #(.width(16), .max('hffff), .ongoal("wrap"), .trigger("rising"), .behavior("new")) counter_1 (
    .count(or_1_out), .Q(\总周期数 ), .clk(CLK));  // open: load, D, carry, clr, preset, down
  Comparator #(.width(16), .mode("twosComplement")) comparator_1 (
    .a(16'h23b), .b(\总周期数 ), .eq(comparator_1_eq));  // open: gt, lt
  Comparator #(.width(16), .mode("twosComplement")) comparator_2 (
    .a(\总周期数 ), .b(16'h1), .eq(comparator_2_eq));  // open: gt, lt
  Comparator #(.width(16), .mode("twosComplement")) comparator_3 (
    .a(\总周期数 ), .b(16'h4), .eq(comparator_3_eq));  // open: gt, lt
  Comparator #(.width(16), .mode("twosComplement")) comparator_4 (
    .a(\总周期数 ), .b(16'h7), .eq(comparator_4_eq));  // open: gt, lt
  Hex_Digit_Display hex_digit_display_5 (.value(LedData[15:12]));  // open: dp
  Hex_Digit_Display hex_digit_display_6 (.value(LedData[11:8]));  // open: dp
  or or_2 (or_2_out, comparator_1_eq, comparator_2_eq);
  assign IRA = or_2_out ? ~CLK : 1'bz;  // Controlled_Inverter controlled_inverter_1
  assign IRB = comparator_3_eq ? ~CLK : 1'bz;  // Controlled_Inverter controlled_inverter_2
  assign IRC = comparator_4_eq ? ~CLK : 1'bz;  // Controlled_Inverter controlled_inverter_3
  Hex_Digit_Display hex_digit_display_7 (.value(LedData[3:0]));  // open: dp
  Hex_Digit_Display hex_digit_display_8 (.value(LedData[7:4]));  // open: dp
  // Probe on \总周期数 
  Pull_Resistor #(.pull(0)) pull_resistor_1 (.node(IRA));
  Pull_Resistor #(.pull(0)) pull_resistor_2 (.node(IRB));
  Pull_Resistor #(.pull(0)) pull_resistor_3 (.node(IRC));
  Priority_Encoder #(.select(2), .disabled("Z")) priority_encoder_1 (
    .in0(INTR1), .in1(INTR2), .in2(INTR3), .out(priority_encoder_1_out));  // open: in3, gs, en_out, en_in
  Priority_Encoder #(.select(2), .disabled("Z")) priority_encoder_2 (
    .in0(1'b1), .in1(JALR), .in2(JAL), .in3(Btype), .out(priority_encoder_2_out));  // open: gs, en_out, en_in
  Multiplexer #(.select(2), .width(32), .disabled("Z"), .enable("false")) multiplexer_1 (
    .in0(PC_4), .in1({ALUres[31:12], Addr, ALUres[1:0]}), .in2(PC_J), .in3(PC_B), .out(multiplexer_1_out),
    .sel(priority_encoder_2_out));
  Multiplexer #(.select(2), .width(32), .disabled("Z"), .enable("false")) multiplexer_2 (
    .in0(32'h30ac), .in1(32'h3150), .in2(32'h31f4), .out(IR_PC), .sel(priority_encoder_1_out));  // open: in3
  or or_3 (IR1_t, IR1, IRA);
  and and_1 (and_1_out, Beq, ALUeq);
  not not_2 (not_2_out, ALUeq);
  and and_2 (and_2_out, not_2_out, Bne);
  Priority_Encoder #(.select(2), .disabled("Z")) priority_encoder_3 (
    .in0(1'b1), .in1(INTR), .in2(URET), .out(priority_encoder_3_out));  // open: in3, gs, en_out, en_in
  or or_4 (W1, INTR1, d_ff_1_q);
  or or_5 (IR2_t, IR2, IRB);
  Register #(.width(32), .trigger("rising"), .Select("low")) register_1 (
    .D(multiplexer_1_out), .en(INTR), .Q(MEPC), .clk(CLK));  // open: clr
  Multiplexer #(.select(2), .width(32), .disabled("Z"), .enable("false")) multiplexer_3 (
    .in0(multiplexer_1_out), .in1(IR_PC), .in2(MEPC), .out(multiplexer_3_out), .sel(priority_encoder_3_out));  // open: in3
  D_Flip_Flop #(.trigger("rising"), .Pre_Clr_Positions("LEGACY"), .NegatePresetClear("false"), .enable("true"), .NewFFLayout("false")) d_ff_1 (
    .clk(IRA), .D(1'b1), .Q(d_ff_1_q), .reset(INTR1));  // open: Qn, preset, en
  Register #(.width(2), .trigger("rising"), .Select("low")) register_2 (
    .D(priority_encoder_1_out), .en(INTR), .Q(register_2_q), .clk(CLK));  // open: clr
  or or_6 (Btype, and_1_out, and_2_out);
  or or_7 (or_7_out, Go, not_3_out);
  not not_3 (not_3_out, halt);
  or or_8 (IRHAVE, INTR1, INTR2, INTR3);
  or or_9 (or_9_out, d_ff_1_q, INTR1);
  Demultiplexer #(.select(2), .width(1), .tristate("false"), .disabled("Z"), .enable("false")) demultiplexer_1 (
    .out0(CLR1), .out1(CLR2), .out2(CLR3), .in(URET), .sel(register_2_q));  // open: out3
  or or_10 (IR3_t, IR3, IRC);
  Register #(.width(32), .trigger("rising"), .Select("low")) u_PC (
    .D(multiplexer_3_out), .en(or_7_out), .Q(PC), .clk(CLK), .clr(RST));
  and and_3 (and_3_out, or_9_out, ~CLR1);  // AND_Gate
  or or_11 (Jtype, JAL, JALR);
  and and_4 (INTR, IE, IRHAVE);
  D_Flip_Flop #(.trigger("rising"), .Pre_Clr_Positions("LEGACY"), .NegatePresetClear("false"), .enable("true"), .NewFFLayout("false")) u_IR1 (
    .clk(CLK), .D(and_3_out), .Q(INTR1));  // open: Qn, preset, en, reset
  // RiscV_Probe riscv_probe_1: pin names not known; wires that end beside it: IR
  Adder #(.width(32)) adder_1 (.a(PC), .b(32'h4), .out(PC_4));  // open: cin, cout
  ROM #(.addrWidth(10), .dataWidth(32), .Select("high")) rom_1 (.addr(PC[11:2]), .data(IR));
  or or_12 (W2, INTR2, d_ff_2_q);
  \单周期硬布线控制器  \u_单周期硬布线控制器_1  (
    .OP(IR[6:2]), .Funct({IR[30], IR[25], IR[14:12]}), .ALU_OP(\单周期硬布线控制器_1_alu_op ), .in_3(IR[21]),
    .uret(URET), .MemToReg(MemToReg), .ecall(ecall), .MemWrite(MemWrite), .ALU_SRC(\单周期硬布线控制器_1_alu_src ),
    .RegWrite(RegWrite), .S_type(Stype), .Beq(Beq), .Bne(Bne), .Jalr(JALR), .JAL(JAL));  // open: CSRRCI, CSRRSI
  Multiplexer #(.select(1), .width(5), .disabled("Z"), .enable("false")) multiplexer_4 (
    .in0(IR[19:15]), .in1(5'b10001), .out(multiplexer_4_out), .sel(ecall));
  Multiplexer #(.select(1), .width(5), .disabled("Z"), .enable("false")) multiplexer_5 (
    .in0(IR[24:20]), .in1(5'b01010), .out(multiplexer_5_out), .sel(ecall));
  assign bit_extender_1_out = {{20{IR[31]}}, IR[31:20]};  // Bit_Extender bit_extender_1
  assign bit_extender_2_out = {{20{IR[31]}}, {IR[31:25], IR[11:7]}};  // Bit_Extender bit_extender_2
  D_Flip_Flop #(.trigger("rising"), .Pre_Clr_Positions("LEGACY"), .NegatePresetClear("false"), .enable("true"), .NewFFLayout("false")) d_ff_2 (
    .clk(IRB), .D(1'b1), .Q(d_ff_2_q), .reset(INTR2));  // open: Qn, preset, en
  Multiplexer #(.select(1), .width(32), .disabled("Z"), .enable("false")) multiplexer_6 (
    .in0(bit_extender_1_out), .in1(bit_extender_2_out), .out(multiplexer_6_out), .sel(Stype));
  assign bit_extender_3_out = {{20{IR[31]}}, {IR[31], IR[7], IR[30:25], IR[11:8]}};  // Bit_Extender bit_extender_3
  assign bit_extender_4_out = {{12{IR[31]}}, {IR[31], IR[19:12], IR[20], IR[30:21]}};  // Bit_Extender bit_extender_4
  or or_13 (or_13_out, d_ff_2_q, INTR2);
  D_Flip_Flop #(.trigger("high"), .Pre_Clr_Positions("LEGACY"), .NegatePresetClear("false"), .enable("true"), .NewFFLayout("false")) d_ff_3 (.Q(d_ff_3_q));  // open: clk, D, Qn, preset, en, reset
  // Probe on 13'hc
  Regifile regifile_1 (
    .Din(RDin), .Clk(CLK), .R1(regifile_1_r1), .R2(a1), .WE(RegWrite), .W_num(IR[11:7]),
    .R1_num(multiplexer_4_out), .R2_num(multiplexer_5_out));
  Shifter #(.width(32), .shift("ll")) shifter_1 (.in(bit_extender_3_out), .\dist (5'b00001), .out(shifter_1_out));
  Shifter #(.width(32), .shift("ll")) shifter_2 (.in(bit_extender_4_out), .\dist (5'b00001), .out(shifter_2_out));
  and and_5 (and_5_out, or_13_out, ~CLR2);  // AND_Gate
  Comparator #(.width(13), .mode("twosComplement")) comparator_5 (
    .a(CNT_num), .b(13'hc), .eq(comparator_5_eq), .lt(comparator_5_lt));  // open: gt
  Clock #(.highDuration(1), .lowDuration(1)) clock_1 (.out(clock_1_out));
  Multiplexer #(.select(1), .width(32), .disabled("Z"), .enable("false")) multiplexer_7 (
    .in0(a1), .in1(multiplexer_6_out), .out(multiplexer_7_out), .sel(\单周期硬布线控制器_1_alu_src ));
  Adder #(.width(32)) adder_2 (.a(shifter_1_out), .b(PC), .out(PC_B));  // open: cin, cout
  Adder #(.width(32)) adder_3 (.a(shifter_2_out), .b(PC), .out(PC_J));  // open: cin, cout
  D_Flip_Flop #(.trigger("rising"), .Pre_Clr_Positions("LEGACY"), .NegatePresetClear("false"), .enable("true"), .NewFFLayout("false")) u_IR2 (
    .clk(CLK), .D(and_5_out), .Q(INTR2));  // open: Qn, preset, en, reset
  nand nand_1 (nand_1_out, d_ff_3_q, comparator_5_eq);
  Counter #(.width(13), .max('h1fff), .ongoal("stay"), .trigger("rising"), .behavior("old")) counter_2 (
    .count(comparator_5_lt), .Q(CNT_num), .clk(clock_1_out));  // open: load, D, carry, clr, preset
  ALU alu_1 (
    .X(regifile_1_r1), .Y(multiplexer_7_out), .AluOP(\单周期硬布线控制器_1_alu_op ), .Equal(ALUeq),
    .Result({ALUres[31:12], Addr, ALUres[1:0]}), .out_4(ALUge), .out_6(ALUle));  // open: Result_2
  assign CLK = nand_1_out ? clock_1_out : 1'bz;  // Controlled_Buffer controlled_buffer_1
  Comparator #(.width(32), .mode("twosComplement")) comparator_6 (
    .a(32'h22), .b(regifile_1_r1), .gt(comparator_6_gt), .eq(comparator_6_eq), .lt(comparator_6_lt));
  or or_14 (or_14_out, ~IRHAVE, URET);  // OR_Gate
  Pull_Resistor #(.pull(1)) pull_resistor_4 (.node(CLK));
  Register #(.width(32), .trigger("rising"), .Select("low")) register_3 (
    .D(a1), .en(and_6_out), .Q(LedData), .clk(CLK));  // open: clr
  and and_6 (and_6_out, ecall, comparator_6_eq);
  or or_15 (W3, INTR3, d_ff_5_q);
  and and_7 (and_7_out, or_16_out, ecall);
  or or_16 (or_16_out, comparator_6_gt, comparator_6_lt);
  D_Flip_Flop #(.trigger("rising"), .Pre_Clr_Positions("LEGACY"), .NegatePresetClear("false"), .enable("true"), .NewFFLayout("true")) d_ff_4 (
    .clk(CLK), .D(or_14_out), .Q(IE));  // open: Qn, preset, en, reset
  D_Flip_Flop #(.trigger("rising"), .Pre_Clr_Positions("LEGACY"), .NegatePresetClear("false"), .enable("true"), .NewFFLayout("false")) d_ff_5 (
    .clk(IRC), .D(1'b1), .Q(d_ff_5_q), .reset(INTR3));  // open: Qn, preset, en
  RAM #(.addrWidth(10), .dataWidth(32), .bus("separate"), .Select("high")) ram_1 (
    .addr(Addr), .din(a1), .data(Dout), .str(MemWrite), .sel(1'b1), .clk(CLK), .ld(1'b1));  // open: clr
  Multiplexer #(.select(2), .width(32), .disabled("Z"), .enable("false")) multiplexer_8 (
    .in0({ALUres[31:12], Addr, ALUres[1:0]}), .in1(Dout), .in2(PC_4), .in3(PC_4), .out(RDin),
    .sel({Jtype, MemToReg}));
  or or_17 (or_17_out, d_ff_5_q, INTR3);
  D_Flip_Flop #(.trigger("falling"), .Pre_Clr_Positions("ABOVE_BELOW"), .NegatePresetClear("false"), .enable("true"), .NewFFLayout("true")) d_ff_6 (
    .clk(CLK), .D(1'b1), .Q(halt), .en(and_7_out), .reset(Go));  // open: Qn, preset
  and and_8 (and_8_out, or_17_out, ~CLR3);  // AND_Gate
  D_Flip_Flop #(.trigger("rising"), .Pre_Clr_Positions("LEGACY"), .NegatePresetClear("false"), .enable("true"), .NewFFLayout("false")) u_IR3 (
    .clk(CLK), .D(and_8_out), .Q(INTR3));  // open: Qn, preset, en, reset
  Comparator #(.width(10), .mode("twosComplement")) comparator_7 (
    .a(Addr), .b(10'h24), .lt(comparator_7_lt));  // open: gt, eq
  and and_9 (and_9_out, MemWrite, comparator_7_lt);
  Comparator #(.width(32), .mode("twosComplement")) comparator_8 (
    .a(a1), .b(32'hb), .eq(comparator_8_eq));  // open: gt, lt
  MapReg_1 mapreg_1_1 (
    .En(and_9_out), .Addr(Addr), .CLK(CLK), .Data(a1), .\行1 (\mapreg_1_1_行1 ), .\行9 (\mapreg_1_1_行9 ),
    .\行17 (\mapreg_1_1_行17 ), .\行25 (\mapreg_1_1_行25 ), .\行2 (\mapreg_1_1_行2 ), .\行10 (\mapreg_1_1_行10 ),
    .\行18 (\mapreg_1_1_行18 ), .\行26 (\mapreg_1_1_行26 ), .\行3 (\mapreg_1_1_行3 ), .\行11 (\mapreg_1_1_行11 ),
    .\行19 (\mapreg_1_1_行19 ), .\行27 (\mapreg_1_1_行27 ), .\行4 (\mapreg_1_1_行4 ), .\行12 (\mapreg_1_1_行12 ),
    .\行20 (\mapreg_1_1_行20 ), .\行28 (\mapreg_1_1_行28 ), .\行5 (\mapreg_1_1_行5 ), .\行13 (\mapreg_1_1_行13 ),
    .\行21 (\mapreg_1_1_行21 ), .\行29 (\mapreg_1_1_行29 ), .\行6 (\mapreg_1_1_行6 ), .\行14 (\mapreg_1_1_行14 ),
    .\行22 (\mapreg_1_1_行22 ), .\行30 (\mapreg_1_1_行30 ), .\行7 (\mapreg_1_1_行7 ), .\行15 (\mapreg_1_1_行15 ),
    .\行23 (\mapreg_1_1_行23 ), .\行31 (\mapreg_1_1_行31 ), .\行8 (\mapreg_1_1_行8 ), .\行16 (\mapreg_1_1_行16 ),
    .\行24 (\mapreg_1_1_行24 ), .\行32 (\mapreg_1_1_行32 ), .RST(RST));
  and and_10 (and_10_out, comparator_8_eq, ecall);
  MapReg_2 mapreg_2_1 (
    .En(and_10_out), ._1(\mapreg_1_1_行1 ), ._9(\mapreg_1_1_行9 ), ._17(\mapreg_1_1_行17 ),
    ._25(\mapreg_1_1_行25 ), ._2(\mapreg_1_1_行2 ), ._10(\mapreg_1_1_行10 ), ._18(\mapreg_1_1_行18 ),
    ._26(\mapreg_1_1_行26 ), ._3(\mapreg_1_1_行3 ), ._11(\mapreg_1_1_行11 ), ._19(\mapreg_1_1_行19 ),
    ._27(\mapreg_1_1_行27 ), ._4(\mapreg_1_1_行4 ), ._12(\mapreg_1_1_行12 ), ._20(\mapreg_1_1_行20 ),
    ._28(\mapreg_1_1_行28 ), ._5(\mapreg_1_1_行5 ), ._13(\mapreg_1_1_行13 ), ._21(\mapreg_1_1_行21 ),
    ._29(\mapreg_1_1_行29 ), ._6(\mapreg_1_1_行6 ), ._14(\mapreg_1_1_行14 ), ._22(\mapreg_1_1_行22 ),
    ._30(\mapreg_1_1_行30 ), ._7(\mapreg_1_1_行7 ), ._15(\mapreg_1_1_行15 ), ._23(\mapreg_1_1_行23 ),
    ._31(\mapreg_1_1_行31 ), ._8(\mapreg_1_1_行8 ), ._16(\mapreg_1_1_行16 ), ._24(\mapreg_1_1_行24 ),
    ._32(\mapreg_1_1_行32 ), .CLK(CLK), .\行1 (\行1 ), .\行9 (\行2 ), .\行17 (\行3 ), .\行25 (\行4 ), .\行2 (\行5 ),
    .\行10 (\行6 ), .\行18 (\行7 ), .\行26 (\行8 ), .\行3 (\行9 ), .\行11 (\行10 ), .\行19 (\行11 ), .\行27 (\行12 ),
    .\行4 (\行13 ), .\行12 (\行14 ), .\行20 (\行15 ), .\行28 (\行16 ), .\行5 (\行17 ), .\行13 (\行18 ), .\行21 (\行19 ),
    .\行29 (\行20 ), .\行6 (\行21 ), .\行14 (\行22 ), .\行22 (\行23 ), .\行30 (\行24 ), .\行7 (\行25 ), .\行15 (\行26 ),
    .\行23 (\行27 ), .\行31 (\行28 ), .\行8 (\行29 ), .\行16 (\行30 ), .\行24 (\行31 ), .\行32 (\行32 ), .RST(RST));

  // Other names for the same wires on the sheet: ALUres[11:2] = Addr; MDin[31:0] = a1

  // Notes on the sheet:
  //   中断源
  //   中断等待指示
  //   总复位信号应将除ROM以外所有存储组件全部清零
  //   单级中断测试信号模拟器
  //   数码管输出
  //   数码管输出应该用寄存器锁存，否则显示数据只能一闪而过
  //   中断响应阶段
  //   指令探针
  //   指令存储器
  //   中断响应
  //   为方便自动评测，需要输出PC，IR，寄存器堆写如数据RDin
  //   RAM写使能MemWrite、RAM写入数据MDin等信号
  //   指令字
  //   contents of rom_1 (hex, n*v repeats v):
  //   7d000113 100413 1f41993 41f9d993 433 c00913 800b13 140413 f47413 800293 100313 499993 89e9b3 1300533
  //   2200893 73 406282b3 fe0294e3 140413 f00f93 1f47433 1c41413 800293 100313 49d993 89e9b3 1300533
  //   2200893 73 406282b3 fe0294e3 1c45413 406b0b33 b0463 f95ff06f 2b3 fff2c293 1029293 fff2e293 500533
  //   2200893 73 f5dff06f 1112023 410113 a12023 410113 812023 410113 1312023 410113 1412023 410113 1512023
  //   410113 1612023 410113 100b13 300a13 100a93 1600433 441413 14469b3 1300533 2200893 73 fe0416e3
  //   415a0a33 fe0a10e3 ffc10113 12b03 ffc10113 12a83 ffc10113 12a03 ffc10113 12983 ffc10113 12403
  //   ffc10113 12503 ffc10113 12883 200073 1112023 410113 a12023 410113 812023 410113 1312023 410113
  //   1412023 410113 1512023 410113 1612023 410113 200b13 300a13 100a93 1600433 441413 14469b3 1300533
  //   2200893 73 fe0416e3 415a0a33 fe0a10e3 ffc10113 12b03 ffc10113 12a83 ffc10113 12a03 ffc10113 12983
  //   ffc10113 12403 ffc10113 12503 ffc10113 12883 200073 1112023 410113 a12023 410113 812023 410113
  //   1312023 410113 1412023 410113 1512023 410113 1612023 410113 300b13 300a13 100a93 1600433 441413
  //   14469b3 1300533 2200893 73 fe0416e3 415a0a33 fe0a10e3 ffc10113 12b03 ffc10113 12a83 ffc10113 12a03
  //   ffc10113 12983 ffc10113 12403 ffc10113 12503 ffc10113 12883 200073
  //   URET
  //   Beq
  //   Bne
  //   MemToReg
  //   MemWrite
  //   AluOP
  //   AluSrcB
  //   RegWrite
  //   控制位
  //   暂停节拍，不能为0
  //   戳工具置1进入计数暂停模式，ctrl+k时钟自动运行到对应节拍暂停
  //   ctrl+k关闭时钟连续运行，将控制位置零，进入单步调试模式调试
  //   中断使能位(用于开关中断)
  //   可计数暂停的时钟源
  //   数据存储器
  //   判断中断使能
endmodule

module \点阵显示  (
  input  \结束 ,
  input  \开始 ,
  input  CLK,
  input  RST,
  input  \上 ,
  input  \下 ,
  output [31:0] _1,
  output [31:0] _2,
  output [31:0] _3,
  output [31:0] _4,
  output [31:0] _5,
  output [31:0] _6,
  output [31:0] _7,
  output [31:0] _8,
  output [31:0] _9,
  output [31:0] _10,
  output [31:0] _11,
  output [31:0] _12,
  output [31:0] _13,
  output [31:0] _14,
  output [31:0] _15,
  output [31:0] _16,
  output [31:0] _17,
  output [31:0] _18,
  output [31:0] _19,
  output [31:0] _20,
  output [31:0] _21,
  output [31:0] _22,
  output [31:0] _23,
  output [31:0] _24,
  output [31:0] _25,
  output [31:0] _26,
  output [31:0] _27,
  output [31:0] _28,
  output [31:0] _29,
  output [31:0] _30,
  output \得分 ,
  output [31:0] _31,
  output [31:0] _32
);

  wire [31:0] and_1_out, and_2_out, and_3_out, and_4_out, and_5_out, and_6_out, and_7_out, and_8_out,
       and_9_out, and_10_out, and_11_out, and_12_out, and_13_out, and_14_out, and_15_out, and_16_out,
       and_17_out, and_18_out, and_19_out, and_20_out, and_21_out, and_22_out, and_23_out, and_24_out,
       and_25_out, and_26_out, and_27_out, and_28_out, or_1_out, or_2_out, or_3_out, or_4_out, or_5_out,
       or_6_out, or_7_out, or_8_out, or_9_out, or_10_out, or_11_out, or_12_out, or_13_out, or_14_out,
       or_15_out, or_16_out, or_17_out, or_18_out, or_19_out, or_20_out, or_21_out, or_22_out, or_23_out,
       or_24_out, or_25_out, or_26_out, or_27_out, or_28_out, or_29_out, or_30_out, or_31_out, or_32_out,
       or_33_out, \玩家移动_1_行1 , \玩家移动_1_行2 , \玩家移动_1_行3 , \玩家移动_1_行4 , \玩家移动_1_行5 , \玩家移动_1_行6 , \玩家移动_1_行7 ,
       \玩家移动_1_行8 , \玩家移动_1_行9 , \玩家移动_1_行10 , \玩家移动_1_行11 , \玩家移动_1_行12 , \玩家移动_1_行13 , \玩家移动_1_行14 ,
       \玩家移动_1_行15 , \玩家移动_1_行16 , \玩家移动_1_行17 , \玩家移动_1_行18 , \玩家移动_1_行19 , \玩家移动_1_行20 , \玩家移动_1_行21 ,
       \玩家移动_1_行22 , \玩家移动_1_行23 , \玩家移动_1_行24 , \玩家移动_1_行25 , \玩家移动_1_行26 , \玩家移动_1_行27 , \玩家移动_1_行28 ,
       \玩家移动_1_行29 , \玩家移动_1_行30 , \玩家移动_1_行31 , \玩家移动_1_行32 , \障碍下落_1_行1 , \障碍下落_1_行2 , \障碍下落_1_行3 ,
       \障碍下落_1_行4 , \障碍下落_1_行5 , \障碍下落_1_行6 , \障碍下落_1_行7 , \障碍下落_1_行8 , \障碍下落_1_行9 , \障碍下落_1_行10 ,
       \障碍下落_1_行11 , \障碍下落_1_行12 , \障碍下落_1_行13 , \障碍下落_1_行14 , \障碍下落_1_行15 , \障碍下落_1_行16 , \障碍下落_1_行17 ,
       \障碍下落_1_行18 , \障碍下落_1_行19 , \障碍下落_1_行20 , \障碍下落_1_行21 , \障碍下落_1_行22 , \障碍下落_1_行23 , \障碍下落_1_行24 ,
       \障碍下落_1_行25 , \障碍下落_1_行26 , \障碍下落_1_行27 , \障碍下落_1_行28 , \障碍下落_1_行29 , \障碍下落_1_行30 , \障碍下落_1_行31 ,
       \障碍下落_1_行32 ;

  \障碍下落  \u_障碍下落_1  (
    .IR3(\开始 ), .RST(RST), .CLK(CLK), .\行1 (\障碍下落_1_行1 ), .\行2 (\障碍下落_1_行2 ), .\行3 (\障碍下落_1_行3 ),
    .\行4 (\障碍下落_1_行4 ), .\行5 (\障碍下落_1_行5 ), .\行6 (\障碍下落_1_行6 ), .\行7 (\障碍下落_1_行7 ), .\行8 (\障碍下落_1_行8 ),
    .\行9 (\障碍下落_1_行9 ), .\行10 (\障碍下落_1_行10 ), .\行11 (\障碍下落_1_行11 ), .\行12 (\障碍下落_1_行12 ),
    .\行13 (\障碍下落_1_行13 ), .\行14 (\障碍下落_1_行14 ), .\行15 (\障碍下落_1_行15 ), .\行16 (\障碍下落_1_行16 ),
    .\行17 (\障碍下落_1_行17 ), .\行18 (\障碍下落_1_行18 ), .\行19 (\障碍下落_1_行19 ), .\行20 (\障碍下落_1_行20 ),
    .\行21 (\障碍下落_1_行21 ), .\行22 (\障碍下落_1_行22 ), .\行23 (\障碍下落_1_行23 ), .\行24 (\障碍下落_1_行24 ),
    .\行25 (\障碍下落_1_行25 ), .\行26 (\障碍下落_1_行26 ), .\行27 (\障碍下落_1_行27 ), .\行28 (\障碍下落_1_行28 ),
    .\行29 (\障碍下落_1_行29 ), .\行30 (\障碍下落_1_行30 ), .\行31 (\障碍下落_1_行31 ), .\行32 (\障碍下落_1_行32 ));  // open: IR1, IR2
  \玩家移动  \u_玩家移动_1  (
    .IR1(\上 ), .IR2(\下 ), .IR3(\开始 ), .RST(RST), .CLK(CLK), .\行1 (\玩家移动_1_行1 ), .\行2 (\玩家移动_1_行2 ),
    .\行3 (\玩家移动_1_行3 ), .\行4 (\玩家移动_1_行4 ), .\行5 (\玩家移动_1_行5 ), .\行6 (\玩家移动_1_行6 ), .\行7 (\玩家移动_1_行7 ),
    .\行8 (\玩家移动_1_行8 ), .\行9 (\玩家移动_1_行9 ), .\行10 (\玩家移动_1_行10 ), .\行11 (\玩家移动_1_行11 ), .\行12 (\玩家移动_1_行12 ),
    .\行13 (\玩家移动_1_行13 ), .\行14 (\玩家移动_1_行14 ), .\行15 (\玩家移动_1_行15 ), .\行16 (\玩家移动_1_行16 ),
    .\行17 (\玩家移动_1_行17 ), .\行18 (\玩家移动_1_行18 ), .\行19 (\玩家移动_1_行19 ), .\行20 (\玩家移动_1_行20 ),
    .\行21 (\玩家移动_1_行21 ), .\行22 (\玩家移动_1_行22 ), .\行23 (\玩家移动_1_行23 ), .\行24 (\玩家移动_1_行24 ),
    .\行25 (\玩家移动_1_行25 ), .\行26 (\玩家移动_1_行26 ), .\行27 (\玩家移动_1_行27 ), .\行28 (\玩家移动_1_行28 ),
    .\行29 (\玩家移动_1_行29 ), .\行30 (\玩家移动_1_行30 ), .\行31 (\玩家移动_1_行31 ), .\行32 (\玩家移动_1_行32 ));
  assign and_1_out = \障碍下落_1_行3  & \玩家移动_1_行3 ;  // AND_Gate and_1, 32 bits wide
  assign and_2_out = \障碍下落_1_行4  & \玩家移动_1_行4 ;  // AND_Gate and_2, 32 bits wide
  assign and_3_out = \障碍下落_1_行6  & \玩家移动_1_行6 ;  // AND_Gate and_3, 32 bits wide
  assign and_4_out = \障碍下落_1_行5  & \玩家移动_1_行5 ;  // AND_Gate and_4, 32 bits wide
  assign and_5_out = \障碍下落_1_行8  & \玩家移动_1_行8 ;  // AND_Gate and_5, 32 bits wide
  assign and_6_out = \障碍下落_1_行9  & \玩家移动_1_行9 ;  // AND_Gate and_6, 32 bits wide
  assign and_7_out = \障碍下落_1_行7  & \玩家移动_1_行7 ;  // AND_Gate and_7, 32 bits wide
  assign and_8_out = \障碍下落_1_行11  & \玩家移动_1_行11 ;  // AND_Gate and_8, 32 bits wide
  assign and_9_out = \障碍下落_1_行10  & \玩家移动_1_行10 ;  // AND_Gate and_9, 32 bits wide
  assign and_10_out = \障碍下落_1_行12  & \玩家移动_1_行12 ;  // AND_Gate and_10, 32 bits wide
  assign and_11_out = \障碍下落_1_行14  & \玩家移动_1_行14 ;  // AND_Gate and_11, 32 bits wide
  assign and_12_out = \障碍下落_1_行13  & \玩家移动_1_行13 ;  // AND_Gate and_12, 32 bits wide
  assign and_13_out = \障碍下落_1_行15  & \玩家移动_1_行15 ;  // AND_Gate and_13, 32 bits wide
  assign and_14_out = \障碍下落_1_行17  & \玩家移动_1_行17 ;  // AND_Gate and_14, 32 bits wide
  assign and_15_out = \障碍下落_1_行16  & \玩家移动_1_行16 ;  // AND_Gate and_15, 32 bits wide
  assign and_16_out = \障碍下落_1_行18  & \玩家移动_1_行18 ;  // AND_Gate and_16, 32 bits wide
  assign or_1_out = and_1_out | and_2_out | and_4_out | and_3_out | and_7_out | and_5_out | and_6_out | and_9_out | and_8_out | and_10_out | and_12_out | and_11_out | and_13_out | and_15_out | and_14_out | and_16_out | and_17_out | and_19_out | and_20_out | and_18_out | and_22_out | and_21_out | and_23_out | and_24_out | and_25_out | and_28_out | and_26_out | and_27_out;  // OR_Gate or_1, 32 bits wide
  Comparator #(.width(32), .mode("unsigned")) comparator_1 (.a(or_1_out), .b({32{1'b0}}), .gt(\得分 ));  // open: eq, lt
  assign and_17_out = \障碍下落_1_行30  & \玩家移动_1_行30 ;  // AND_Gate and_17, 32 bits wide
  assign and_18_out = \障碍下落_1_行27  & \玩家移动_1_行27 ;  // AND_Gate and_18, 32 bits wide
  assign and_19_out = \障碍下落_1_行29  & \玩家移动_1_行29 ;  // AND_Gate and_19, 32 bits wide
  assign and_20_out = \障碍下落_1_行28  & \玩家移动_1_行28 ;  // AND_Gate and_20, 32 bits wide
  assign and_21_out = \障碍下落_1_行25  & \玩家移动_1_行25 ;  // AND_Gate and_21, 32 bits wide
  assign and_22_out = \障碍下落_1_行26  & \玩家移动_1_行26 ;  // AND_Gate and_22, 32 bits wide
  assign and_23_out = \障碍下落_1_行24  & \玩家移动_1_行24 ;  // AND_Gate and_23, 32 bits wide
  assign and_24_out = \障碍下落_1_行23  & \玩家移动_1_行23 ;  // AND_Gate and_24, 32 bits wide
  assign and_25_out = \障碍下落_1_行22  & \玩家移动_1_行22 ;  // AND_Gate and_25, 32 bits wide
  assign or_2_out = \障碍下落_1_行1  | \玩家移动_1_行1 ;  // OR_Gate or_2, 32 bits wide
  assign or_3_out = \障碍下落_1_行2  | \玩家移动_1_行2 ;  // OR_Gate or_3, 32 bits wide
  assign or_4_out = \障碍下落_1_行3  | \玩家移动_1_行3 ;  // OR_Gate or_4, 32 bits wide
  assign or_5_out = \障碍下落_1_行4  | \玩家移动_1_行4 ;  // OR_Gate or_5, 32 bits wide
  assign or_6_out = \障碍下落_1_行5  | \玩家移动_1_行5 ;  // OR_Gate or_6, 32 bits wide
  assign or_7_out = \障碍下落_1_行6  | \玩家移动_1_行6 ;  // OR_Gate or_7, 32 bits wide
  assign or_8_out = \障碍下落_1_行7  | \玩家移动_1_行7 ;  // OR_Gate or_8, 32 bits wide
  assign or_9_out = \障碍下落_1_行8  | \玩家移动_1_行8 ;  // OR_Gate or_9, 32 bits wide
  assign or_10_out = \障碍下落_1_行9  | \玩家移动_1_行9 ;  // OR_Gate or_10, 32 bits wide
  assign or_11_out = \障碍下落_1_行10  | \玩家移动_1_行10 ;  // OR_Gate or_11, 32 bits wide
  assign or_12_out = \障碍下落_1_行11  | \玩家移动_1_行11 ;  // OR_Gate or_12, 32 bits wide
  assign or_13_out = \障碍下落_1_行12  | \玩家移动_1_行12 ;  // OR_Gate or_13, 32 bits wide
  assign or_14_out = \障碍下落_1_行13  | \玩家移动_1_行13 ;  // OR_Gate or_14, 32 bits wide
  assign or_15_out = \障碍下落_1_行14  | \玩家移动_1_行14 ;  // OR_Gate or_15, 32 bits wide
  assign or_16_out = \障碍下落_1_行15  | \玩家移动_1_行15 ;  // OR_Gate or_16, 32 bits wide
  assign or_17_out = \障碍下落_1_行16  | \玩家移动_1_行16 ;  // OR_Gate or_17, 32 bits wide
  assign and_26_out = \障碍下落_1_行20  & \玩家移动_1_行20 ;  // AND_Gate and_26, 32 bits wide
  assign and_27_out = \障碍下落_1_行19  & \玩家移动_1_行19 ;  // AND_Gate and_27, 32 bits wide
  assign and_28_out = \障碍下落_1_行21  & \玩家移动_1_行21 ;  // AND_Gate and_28, 32 bits wide
  assign or_18_out = \玩家移动_1_行17  | \障碍下落_1_行17 ;  // OR_Gate or_18, 32 bits wide
  assign or_19_out = \玩家移动_1_行18  | \障碍下落_1_行18 ;  // OR_Gate or_19, 32 bits wide
  assign or_20_out = \玩家移动_1_行19  | \障碍下落_1_行19 ;  // OR_Gate or_20, 32 bits wide
  assign or_21_out = \玩家移动_1_行20  | \障碍下落_1_行20 ;  // OR_Gate or_21, 32 bits wide
  assign or_22_out = \玩家移动_1_行21  | \障碍下落_1_行21 ;  // OR_Gate or_22, 32 bits wide
  assign or_23_out = \玩家移动_1_行22  | \障碍下落_1_行22 ;  // OR_Gate or_23, 32 bits wide
  assign or_24_out = \玩家移动_1_行23  | \障碍下落_1_行23 ;  // OR_Gate or_24, 32 bits wide
  assign or_25_out = \玩家移动_1_行24  | \障碍下落_1_行24 ;  // OR_Gate or_25, 32 bits wide
  assign or_26_out = \玩家移动_1_行25  | \障碍下落_1_行25 ;  // OR_Gate or_26, 32 bits wide
  assign or_27_out = \玩家移动_1_行26  | \障碍下落_1_行26 ;  // OR_Gate or_27, 32 bits wide
  assign or_28_out = \玩家移动_1_行27  | \障碍下落_1_行27 ;  // OR_Gate or_28, 32 bits wide
  assign or_29_out = \玩家移动_1_行28  | \障碍下落_1_行28 ;  // OR_Gate or_29, 32 bits wide
  assign or_30_out = \玩家移动_1_行29  | \障碍下落_1_行29 ;  // OR_Gate or_30, 32 bits wide
  assign or_31_out = \玩家移动_1_行30  | \障碍下落_1_行30 ;  // OR_Gate or_31, 32 bits wide
  assign or_32_out = \玩家移动_1_行31  | \障碍下落_1_行31 ;  // OR_Gate or_32, 32 bits wide
  assign or_33_out = \玩家移动_1_行32  | \障碍下落_1_行32 ;  // OR_Gate or_33, 32 bits wide
  Multiplexer #(.select(1), .width(32), .disabled("Z"), .enable("false")) multiplexer_1 (
    .in0(or_2_out), .in1({32{1'b0}}), .out(_1), .sel(\结束 ));
  Multiplexer #(.select(1), .width(32), .disabled("Z"), .enable("false")) multiplexer_2 (
    .in0(or_3_out), .in1({32{1'b0}}), .out(_2), .sel(\结束 ));
  Multiplexer #(.select(1), .width(32), .disabled("Z"), .enable("false")) multiplexer_3 (
    .in0(or_4_out), .in1({32{1'b0}}), .out(_3), .sel(\结束 ));
  Multiplexer #(.select(1), .width(32), .disabled("Z"), .enable("false")) multiplexer_4 (
    .in0(or_5_out), .in1({32{1'b0}}), .out(_4), .sel(\结束 ));
  Multiplexer #(.select(1), .width(32), .disabled("Z"), .enable("false")) multiplexer_5 (
    .in0(or_18_out), .in1(32'h20089204), .out(_17), .sel(\结束 ));
  Multiplexer #(.select(1), .width(32), .disabled("Z"), .enable("false")) multiplexer_6 (
    .in0(or_6_out), .in1({32{1'b0}}), .out(_5), .sel(\结束 ));
  Multiplexer #(.select(1), .width(32), .disabled("Z"), .enable("false")) multiplexer_7 (
    .in0(or_7_out), .in1({32{1'b0}}), .out(_6), .sel(\结束 ));
  Multiplexer #(.select(1), .width(32), .disabled("Z"), .enable("false")) multiplexer_8 (
    .in0(or_13_out), .in1(32'h200a1220), .out(_12), .sel(\结束 ));
  Multiplexer #(.select(1), .width(32), .disabled("Z"), .enable("false")) multiplexer_9 (
    .in0(or_19_out), .in1(32'h20089204), .out(_18), .sel(\结束 ));
  Multiplexer #(.select(1), .width(32), .disabled("Z"), .enable("false")) multiplexer_10 (
    .in0(or_8_out), .in1({32{1'b0}}), .out(_7), .sel(\结束 ));
  Multiplexer #(.select(1), .width(32), .disabled("Z"), .enable("false")) multiplexer_11 (
    .in0(or_14_out), .in1(32'h200a1210), .out(_13), .sel(\结束 ));
  Multiplexer #(.select(1), .width(32), .disabled("Z"), .enable("false")) multiplexer_12 (
    .in0(or_20_out), .in1(32'h20089208), .out(_19), .sel(\结束 ));
  Multiplexer #(.select(1), .width(32), .disabled("Z"), .enable("false")) multiplexer_13 (
    .in0(or_21_out), .in1(32'h20085210), .out(_20), .sel(\结束 ));
  Multiplexer #(.select(1), .width(32), .disabled("Z"), .enable("false")) multiplexer_14 (
    .in0(or_25_out), .in1(32'h3fc81300), .out(_24), .sel(\结束 ));
  Multiplexer #(.select(1), .width(32), .disabled("Z"), .enable("false")) multiplexer_15 (
    .in0(or_9_out), .in1({32{1'b0}}), .out(_8), .sel(\结束 ));
  Multiplexer #(.select(1), .width(32), .disabled("Z"), .enable("false")) multiplexer_16 (
    .in0(or_15_out), .in1(32'h20091208), .out(_14), .sel(\结束 ));
  Multiplexer #(.select(1), .width(32), .disabled("Z"), .enable("false")) multiplexer_17 (
    .in0(or_26_out), .in1({32{1'b0}}), .out(_25), .sel(\结束 ));
  Multiplexer #(.select(1), .width(32), .disabled("Z"), .enable("false")) multiplexer_18 (
    .in0(or_27_out), .in1({32{1'b0}}), .out(_26), .sel(\结束 ));
  Multiplexer #(.select(1), .width(32), .disabled("Z"), .enable("false")) multiplexer_19 (
    .in0(or_28_out), .in1({32{1'b0}}), .out(_27), .sel(\结束 ));
  Multiplexer #(.select(1), .width(32), .disabled("Z"), .enable("false")) multiplexer_20 (
    .in0(or_29_out), .in1({32{1'b0}}), .out(_28), .sel(\结束 ));
  Multiplexer #(.select(1), .width(32), .disabled("Z"), .enable("false")) multiplexer_21 (
    .in0(or_30_out), .in1({32{1'b0}}), .out(_29), .sel(\结束 ));
  Multiplexer #(.select(1), .width(32), .disabled("Z"), .enable("false")) multiplexer_22 (
    .in0(or_31_out), .in1({32{1'b0}}), .out(_30), .sel(\结束 ));
  Multiplexer #(.select(1), .width(32), .disabled("Z"), .enable("false")) multiplexer_23 (
    .in0(or_32_out), .in1({32{1'b0}}), .out(_31), .sel(\结束 ));
  Multiplexer #(.select(1), .width(32), .disabled("Z"), .enable("false")) multiplexer_24 (
    .in0(or_33_out), .in1({32{1'b0}}), .out(_32), .sel(\结束 ));
  Multiplexer #(.select(1), .width(32), .disabled("Z"), .enable("false")) multiplexer_25 (
    .in0(or_16_out), .in1(32'h20091204), .out(_15), .sel(\结束 ));
  Multiplexer #(.select(1), .width(32), .disabled("Z"), .enable("false")) multiplexer_26 (
    .in0(or_10_out), .in1(32'h3fc81300), .out(_9), .sel(\结束 ));
  Multiplexer #(.select(1), .width(32), .disabled("Z"), .enable("false")) multiplexer_27 (
    .in0(or_17_out), .in1(32'h3fc91204), .out(_16), .sel(\结束 ));
  Multiplexer #(.select(1), .width(32), .disabled("Z"), .enable("false")) multiplexer_28 (
    .in0(or_22_out), .in1(32'h20085220), .out(_21), .sel(\结束 ));
  Multiplexer #(.select(1), .width(32), .disabled("Z"), .enable("false")) multiplexer_29 (
    .in0(or_11_out), .in1(32'h200c1280), .out(_10), .sel(\结束 ));
  Multiplexer #(.select(1), .width(32), .disabled("Z"), .enable("false")) multiplexer_30 (
    .in0(or_23_out), .in1(32'h20085240), .out(_22), .sel(\结束 ));
  Multiplexer #(.select(1), .width(32), .disabled("Z"), .enable("false")) multiplexer_31 (
    .in0(or_12_out), .in1(32'h200a1240), .out(_11), .sel(\结束 ));
  Multiplexer #(.select(1), .width(32), .disabled("Z"), .enable("false")) multiplexer_32 (
    .in0(or_24_out), .in1(32'h20083280), .out(_23), .sel(\结束 ));
endmodule

// 单周期硬布线控制器
module \单周期硬布线控制器  (
  input  [4:0] OP,
  input  [4:0] Funct,
  input  in_3,
  output [3:0] ALU_OP,
  output uret,
  output MemToReg,
  output ecall,
  output MemWrite,
  output ALU_SRC,
  output RegWrite,
  output S_type,
  output Beq,
  output Bne,
  output Jalr,
  output JAL,
  output CSRRSI,
  output CSRRCI
);

  wire \控制信号自动生成_1_ecall ;

  \运算控制器自动生成  \u_运算控制器自动生成_1  (
    .OP2(OP[0]), .OP3(OP[1]), .OP4(OP[2]), .OP5(OP[3]), .OP6(OP[4]), .F12(Funct[0]), .F13(Funct[1]),
    .F14(Funct[2]), .F25(Funct[3]), .F30(Funct[4]), .S0(ALU_OP[0]), .S1(ALU_OP[1]), .S2(ALU_OP[2]),
    .S3(ALU_OP[3]));
  \控制信号自动生成  \u_控制信号自动生成_1  (
    .OP2(OP[0]), .OP3(OP[1]), .OP4(OP[2]), .OP5(OP[3]), .MemToReg(MemToReg), .OP6(OP[4]), .F12(Funct[0]),
    .F13(Funct[1]), .F14(Funct[2]), .F25(Funct[3]), .F30(Funct[4]), .MemWrite(MemWrite), .ALU_SRC(ALU_SRC),
    .RegWrite(RegWrite), .ecall(\控制信号自动生成_1_ecall ), .S_Type(S_type), .BEQ(Beq), .BNE(Bne), .JAL(Jalr),
    .JALR(JAL), .CSRRSI(CSRRSI), .CSRRCI(CSRRCI));
  and and_1 (uret, in_3, \控制信号自动生成_1_ecall );
  and and_2 (ecall, ~in_3, \控制信号自动生成_1_ecall );  // AND_Gate

  // Other names for the same wires on the sheet: IR21 = in_3; OP_CODE[4:0] = OP

  // Notes on the sheet:
  //   运算器控制器，根据指令生成运算器功能选择信号
endmodule

// 运算器控制器
module \运算控制器自动生成  (
  input  OP2,
  input  OP3,
  input  OP4,
  input  OP5,
  input  OP6,
  input  F12,
  input  F13,
  input  F14,
  input  F25,
  input  F30,
  output S0,
  output S1,
  output S2,
  output S3
);

  wire and_1_out, and_2_out, and_3_out, and_4_out, and_5_out, and_6_out, and_7_out, and_8_out, and_9_out,
       and_10_out, and_11_out, and_12_out, and_13_out, and_14_out, and_15_out, and_16_out, and_17_out,
       and_18_out, and_19_out, and_20_out, and_21_out, and_22_out, and_23_out, and_24_out, and_25_out,
       and_26_out, and_27_out, and_28_out, and_29_out, and_30_out, and_31_out, and_32_out, and_33_out,
       and_34_out, and_35_out, and_36_out, and_37_out, and_38_out, and_39_out, and_40_out, and_41_out,
       and_42_out, and_43_out, not_1_out, not_2_out, not_3_out, not_4_out, not_5_out, not_6_out, not_7_out,
       not_8_out, not_9_out, not_10_out, not_11_out, not_12_out, not_13_out, not_14_out, not_15_out,
       not_16_out, not_17_out, not_18_out, not_19_out, not_20_out, not_21_out, not_22_out, not_23_out,
       not_24_out, not_25_out, not_26_out, not_27_out, not_28_out, not_29_out, not_30_out, not_31_out,
       not_32_out, not_33_out, not_34_out, not_35_out, not_36_out, not_37_out, not_38_out, not_39_out,
       not_40_out, not_41_out, not_42_out, not_43_out, not_44_out, not_45_out, not_46_out, not_47_out,
       not_48_out, not_49_out, not_50_out, not_51_out, not_52_out, not_53_out, not_54_out, not_55_out,
       not_56_out, not_57_out, not_58_out, not_59_out, not_60_out, not_61_out, not_62_out, not_63_out,
       not_64_out, not_65_out, not_66_out, not_67_out, not_68_out, not_69_out, not_70_out, not_71_out,
       not_72_out, not_73_out, not_74_out, not_75_out, not_76_out, not_77_out, not_78_out, not_79_out,
       not_80_out, not_81_out, not_82_out, not_83_out, not_84_out, not_85_out, not_86_out, not_87_out,
       not_88_out, not_89_out, not_90_out, not_91_out, not_92_out, not_93_out, not_94_out, not_95_out,
       not_96_out, not_97_out, not_98_out, not_99_out, not_100_out, not_101_out, not_102_out, not_103_out,
       not_104_out, not_105_out, not_106_out, not_107_out, not_108_out, not_109_out, not_110_out,
       not_111_out, not_112_out, not_113_out, not_114_out, not_115_out, not_116_out, not_117_out,
       not_118_out, not_119_out, not_120_out, not_121_out, not_122_out, not_123_out, not_124_out,
       not_125_out, not_126_out, not_127_out, not_128_out, not_129_out, not_130_out, not_131_out,
       not_132_out, not_133_out, not_134_out, not_135_out, not_136_out, not_137_out, not_138_out,
       not_139_out, not_140_out, not_141_out, not_142_out, not_143_out, not_144_out, not_145_out,
       not_146_out, not_147_out, not_148_out, not_149_out, not_150_out, not_151_out, not_152_out,
       not_153_out, not_154_out, not_155_out, not_156_out, not_157_out, not_158_out, not_159_out,
       not_160_out, not_161_out, not_162_out, not_163_out, not_164_out, not_165_out, not_166_out,
       not_167_out, not_168_out, not_169_out, not_170_out, not_171_out, not_172_out, not_173_out,
       not_174_out, not_175_out, not_176_out, not_177_out, not_178_out, not_179_out, not_180_out,
       not_181_out, not_182_out, not_183_out, not_184_out, not_185_out, not_186_out, not_187_out,
       not_188_out, not_189_out, not_190_out, not_191_out, not_192_out, not_193_out, not_194_out,
       not_195_out, not_196_out, not_197_out, not_198_out, not_199_out, not_200_out, not_201_out,
       not_202_out, not_203_out, not_204_out, not_205_out, not_206_out, not_207_out, not_208_out,
       not_209_out, not_210_out, not_211_out, not_212_out, not_213_out, not_214_out, not_215_out,
       not_216_out, not_217_out, not_218_out, not_219_out, not_220_out, not_221_out, not_222_out,
       not_223_out, not_224_out, not_225_out, not_226_out, not_227_out, not_228_out;

  not not_1 (not_1_out, F30);
  not not_2 (not_2_out, F25);
  not not_3 (not_3_out, F14);
  not not_4 (not_4_out, F13);
  not not_5 (not_5_out, F12);
  not not_6 (not_6_out, OP6);
  not not_7 (not_7_out, OP3);
  not not_8 (not_8_out, OP2);
  not not_9 (not_9_out, F30);
  not not_10 (not_10_out, F25);
  not not_11 (not_11_out, OP6);
  not not_12 (not_12_out, OP3);
  not not_13 (not_13_out, OP2);
  not not_14 (not_14_out, F30);
  not not_15 (not_15_out, F25);
  not not_16 (not_16_out, F14);
  not not_17 (not_17_out, F12);
  not not_18 (not_18_out, OP6);
  not not_19 (not_19_out, OP3);
  not not_20 (not_20_out, OP2);
  not not_21 (not_21_out, F14);
  not not_22 (not_22_out, F13);
  not not_23 (not_23_out, F12);
  not not_24 (not_24_out, OP6);
  not not_25 (not_25_out, OP5);
  not not_26 (not_26_out, OP3);
  not not_27 (not_27_out, OP2);
  not not_28 (not_28_out, OP6);
  not not_29 (not_29_out, OP5);
  not not_30 (not_30_out, OP3);
  not not_31 (not_31_out, OP2);
  not not_32 (not_32_out, F13);
  not not_33 (not_33_out, F12);
  not not_34 (not_34_out, OP6);
  not not_35 (not_35_out, OP5);
  not not_36 (not_36_out, OP3);
  not not_37 (not_37_out, OP2);
  not not_38 (not_38_out, F14);
  not not_39 (not_39_out, F12);
  not not_40 (not_40_out, OP6);
  not not_41 (not_41_out, OP5);
  not not_42 (not_42_out, OP3);
  not not_43 (not_43_out, OP2);
  not not_44 (not_44_out, F25);
  not not_45 (not_45_out, F13);
  not not_46 (not_46_out, OP6);
  not not_47 (not_47_out, OP5);
  not not_48 (not_48_out, OP3);
  not not_49 (not_49_out, OP2);
  not not_50 (not_50_out, F14);
  not not_51 (not_51_out, F12);
  not not_52 (not_52_out, OP6);
  not not_53 (not_53_out, OP5);
  not not_54 (not_54_out, OP4);
  not not_55 (not_55_out, OP3);
  not not_56 (not_56_out, OP2);
  not not_57 (not_57_out, F14);
  not not_58 (not_58_out, F12);
  not not_59 (not_59_out, OP6);
  not not_60 (not_60_out, OP4);
  not not_61 (not_61_out, OP3);
  not not_62 (not_62_out, OP2);
  not not_63 (not_63_out, F14);
  not not_64 (not_64_out, F13);
  not not_65 (not_65_out, F12);
  not not_66 (not_66_out, OP4);
  not not_67 (not_67_out, OP3);
  not not_68 (not_68_out, OP3);
  not not_69 (not_69_out, OP2);
  not not_70 (not_70_out, OP6);
  not not_71 (not_71_out, OP3);
  not not_72 (not_72_out, F13);
  not not_73 (not_73_out, OP6);
  not not_74 (not_74_out, OP5);
  not not_75 (not_75_out, OP4);
  not not_76 (not_76_out, OP3);
  not not_77 (not_77_out, OP2);
  not not_78 (not_78_out, OP4);
  not not_79 (not_79_out, OP3);
  not not_80 (not_80_out, OP2);
  not not_81 (not_81_out, F25);
  not not_82 (not_82_out, F14);
  not not_83 (not_83_out, F13);
  not not_84 (not_84_out, F12);
  not not_85 (not_85_out, OP6);
  not not_86 (not_86_out, OP3);
  not not_87 (not_87_out, OP2);
  not not_88 (not_88_out, F30);
  not not_89 (not_89_out, F25);
  not not_90 (not_90_out, OP6);
  not not_91 (not_91_out, OP3);
  not not_92 (not_92_out, OP2);
  not not_93 (not_93_out, F30);
  not not_94 (not_94_out, F25);
  not not_95 (not_95_out, F14);
  not not_96 (not_96_out, F12);
  not not_97 (not_97_out, OP6);
  not not_98 (not_98_out, OP3);
  not not_99 (not_99_out, OP2);
  not not_100 (not_100_out, OP6);
  not not_101 (not_101_out, OP5);
  not not_102 (not_102_out, OP3);
  not not_103 (not_103_out, OP2);
  not not_104 (not_104_out, F14);
  not not_105 (not_105_out, F12);
  not not_106 (not_106_out, OP6);
  not not_107 (not_107_out, OP5);
  not not_108 (not_108_out, OP3);
  not not_109 (not_109_out, OP2);
  not not_110 (not_110_out, F30);
  not not_111 (not_111_out, F25);
  not not_112 (not_112_out, F13);
  not not_113 (not_113_out, OP6);
  not not_114 (not_114_out, OP5);
  not not_115 (not_115_out, OP3);
  not not_116 (not_116_out, OP2);
  not not_117 (not_117_out, OP3);
  not not_118 (not_118_out, OP2);
  not not_119 (not_119_out, OP4);
  not not_120 (not_120_out, OP3);
  not not_121 (not_121_out, OP2);
  not not_122 (not_122_out, F30);
  not not_123 (not_123_out, F25);
  not not_124 (not_124_out, F14);
  not not_125 (not_125_out, F13);
  not not_126 (not_126_out, F12);
  not not_127 (not_127_out, OP6);
  not not_128 (not_128_out, OP3);
  not not_129 (not_129_out, OP2);
  not not_130 (not_130_out, F25);
  not not_131 (not_131_out, F14);
  not not_132 (not_132_out, F13);
  not not_133 (not_133_out, F12);
  not not_134 (not_134_out, OP6);
  not not_135 (not_135_out, OP3);
  not not_136 (not_136_out, OP2);
  not not_137 (not_137_out, F30);
  not not_138 (not_138_out, F25);
  not not_139 (not_139_out, OP6);
  not not_140 (not_140_out, OP3);
  not not_141 (not_141_out, OP2);
  not not_142 (not_142_out, F30);
  not not_143 (not_143_out, F25);
  not not_144 (not_144_out, F14);
  not not_145 (not_145_out, OP6);
  not not_146 (not_146_out, OP3);
  not not_147 (not_147_out, OP2);
  not not_148 (not_148_out, F14);
  not not_149 (not_149_out, F13);
  not not_150 (not_150_out, F12);
  not not_151 (not_151_out, OP6);
  not not_152 (not_152_out, OP5);
  not not_153 (not_153_out, OP3);
  not not_154 (not_154_out, OP2);
  not not_155 (not_155_out, OP6);
  not not_156 (not_156_out, OP5);
  not not_157 (not_157_out, OP3);
  not not_158 (not_158_out, OP2);
  not not_159 (not_159_out, F14);
  not not_160 (not_160_out, F12);
  not not_161 (not_161_out, OP6);
  not not_162 (not_162_out, OP5);
  not not_163 (not_163_out, OP4);
  not not_164 (not_164_out, OP3);
  not not_165 (not_165_out, OP2);
  not not_166 (not_166_out, F14);
  not not_167 (not_167_out, F12);
  not not_168 (not_168_out, OP6);
  not not_169 (not_169_out, OP4);
  not not_170 (not_170_out, OP3);
  not not_171 (not_171_out, OP2);
  not not_172 (not_172_out, F14);
  not not_173 (not_173_out, F13);
  not not_174 (not_174_out, F12);
  not not_175 (not_175_out, OP4);
  not not_176 (not_176_out, OP3);
  not not_177 (not_177_out, OP3);
  not not_178 (not_178_out, OP2);
  not not_179 (not_179_out, F13);
  not not_180 (not_180_out, OP6);
  not not_181 (not_181_out, OP5);
  not not_182 (not_182_out, OP4);
  not not_183 (not_183_out, OP3);
  not not_184 (not_184_out, OP2);
  not not_185 (not_185_out, F30);
  not not_186 (not_186_out, F25);
  not not_187 (not_187_out, F12);
  not not_188 (not_188_out, OP6);
  not not_189 (not_189_out, OP3);
  not not_190 (not_190_out, OP2);
  not not_191 (not_191_out, F30);
  not not_192 (not_192_out, F25);
  not not_193 (not_193_out, F14);
  not not_194 (not_194_out, F12);
  not not_195 (not_195_out, OP6);
  not not_196 (not_196_out, OP3);
  not not_197 (not_197_out, OP2);
  not not_198 (not_198_out, F30);
  not not_199 (not_199_out, F25);
  not not_200 (not_200_out, F14);
  not not_201 (not_201_out, OP6);
  not not_202 (not_202_out, OP3);
  not not_203 (not_203_out, OP2);
  not not_204 (not_204_out, F12);
  not not_205 (not_205_out, OP6);
  not not_206 (not_206_out, OP5);
  not not_207 (not_207_out, OP3);
  not not_208 (not_208_out, OP2);
  not not_209 (not_209_out, F13);
  not not_210 (not_210_out, F12);
  not not_211 (not_211_out, OP6);
  not not_212 (not_212_out, OP5);
  not not_213 (not_213_out, OP3);
  not not_214 (not_214_out, OP2);
  not not_215 (not_215_out, F14);
  not not_216 (not_216_out, F12);
  not not_217 (not_217_out, OP6);
  not not_218 (not_218_out, OP5);
  not not_219 (not_219_out, OP3);
  not not_220 (not_220_out, OP2);
  not not_221 (not_221_out, F12);
  not not_222 (not_222_out, OP3);
  not not_223 (not_223_out, OP2);
  not not_224 (not_224_out, OP6);
  not not_225 (not_225_out, OP3);
  not not_226 (not_226_out, OP4);
  not not_227 (not_227_out, OP3);
  not not_228 (not_228_out, OP2);
  and and_1 (and_1_out, not_1_out, not_2_out, not_3_out, not_4_out, not_5_out, not_6_out, OP5, OP4, not_7_out, not_8_out);
  and and_2 (and_2_out, not_9_out, not_10_out, F14, F13, F12, not_11_out, OP5, OP4, not_12_out, not_13_out);
  and and_3 (and_3_out, not_14_out, not_15_out, not_16_out, F13, not_17_out, not_18_out, OP5, OP4, not_19_out, not_20_out);
  and and_4 (and_4_out, not_21_out, not_22_out, not_23_out, not_24_out, not_25_out, OP4, not_26_out, not_27_out);
  and and_5 (and_5_out, F14, F13, F12, not_28_out, not_29_out, OP4, not_30_out, not_31_out);
  and and_6 (and_6_out, F14, not_32_out, not_33_out, not_34_out, not_35_out, OP4, not_36_out, not_37_out);
  and and_7 (and_7_out, not_38_out, F13, not_39_out, not_40_out, not_41_out, OP4, not_42_out, not_43_out);
  and and_8 (and_8_out, F30, not_44_out, F14, not_45_out, F12, not_46_out, not_47_out, OP4, not_48_out, not_49_out);
  and and_9 (and_9_out, not_50_out, F13, not_51_out, not_52_out, not_53_out, not_54_out, not_55_out, not_56_out);
  and and_10 (and_10_out, not_57_out, F13, not_58_out, not_59_out, OP5, not_60_out, not_61_out, not_62_out);
  and and_11 (and_11_out, not_63_out, not_64_out, not_65_out, OP6, OP5, not_66_out, not_67_out, OP2);
  and and_12 (and_12_out, F14, F13, F12, OP6, OP5, OP4, not_68_out, not_69_out);
  and and_13 (and_13_out, not_70_out, OP5, OP4, not_71_out, OP2);
  and and_14 (and_14_out, F14, not_72_out, F12, not_73_out, not_74_out, not_75_out, not_76_out, not_77_out);
  and and_15 (and_15_out, F14, F13, F12, OP6, OP5, not_78_out, not_79_out, not_80_out);
  and and_16 (and_16_out, F30, not_81_out, not_82_out, not_83_out, not_84_out, not_85_out, OP5, OP4, not_86_out, not_87_out);
  and and_17 (and_17_out, not_88_out, not_89_out, F14, F13, F12, not_90_out, OP5, OP4, not_91_out, not_92_out);
  and and_18 (and_18_out, not_93_out, not_94_out, not_95_out, F13, not_96_out, not_97_out, OP5, OP4, not_98_out, not_99_out);
  and and_19 (and_19_out, F14, F13, F12, not_100_out, not_101_out, OP4, not_102_out, not_103_out);
  and and_20 (and_20_out, not_104_out, F13, not_105_out, not_106_out, not_107_out, OP4, not_108_out, not_109_out);
  and and_21 (and_21_out, not_110_out, not_111_out, F14, not_112_out, F12, not_113_out, not_114_out, OP4, not_115_out, not_116_out);
  and and_22 (and_22_out, F14, F13, F12, OP6, OP5, OP4, not_117_out, not_118_out);
  and and_23 (and_23_out, F14, F13, F12, OP6, OP5, not_119_out, not_120_out, not_121_out);
  and and_24 (and_24_out, not_122_out, not_123_out, not_124_out, not_125_out, not_126_out, not_127_out, OP5, OP4, not_128_out, not_129_out);
  and and_25 (and_25_out, F30, not_130_out, not_131_out, not_132_out, not_133_out, not_134_out, OP5, OP4, not_135_out, not_136_out);
  and and_26 (and_26_out, not_137_out, not_138_out, F14, F13, F12, not_139_out, OP5, OP4, not_140_out, not_141_out);
  and and_27 (and_27_out, not_142_out, not_143_out, not_144_out, F13, F12, not_145_out, OP5, OP4, not_146_out, not_147_out);
  and and_28 (and_28_out, not_148_out, not_149_out, not_150_out, not_151_out, not_152_out, OP4, not_153_out, not_154_out);
  and and_29 (and_29_out, F14, F13, F12, not_155_out, not_156_out, OP4, not_157_out, not_158_out);
  and and_30 (and_30_out, not_159_out, F13, not_160_out, not_161_out, not_162_out, not_163_out, not_164_out, not_165_out);
  and and_31 (and_31_out, not_166_out, F13, not_167_out, not_168_out, OP5, not_169_out, not_170_out, not_171_out);
  and and_32 (and_32_out, not_172_out, not_173_out, not_174_out, OP6, OP5, not_175_out, not_176_out, OP2);
  and and_33 (and_33_out, F14, F13, F12, OP6, OP5, OP4, not_177_out, not_178_out);
  and and_34 (and_34_out, F14, not_179_out, F12, not_180_out, not_181_out, not_182_out, not_183_out, not_184_out);
  and and_35 (and_35_out, not_185_out, not_186_out, F14, F13, not_187_out, not_188_out, OP5, OP4, not_189_out, not_190_out);
  and and_36 (and_36_out, not_191_out, not_192_out, not_193_out, F13, not_194_out, not_195_out, OP5, OP4, not_196_out, not_197_out);
  and and_37 (and_37_out, not_198_out, not_199_out, not_200_out, F13, F12, not_201_out, OP5, OP4, not_202_out, not_203_out);
  and and_38 (and_38_out, F14, F13, not_204_out, not_205_out, not_206_out, OP4, not_207_out, not_208_out);
  and and_39 (and_39_out, F14, not_209_out, not_210_out, not_211_out, not_212_out, OP4, not_213_out, not_214_out);
  and and_40 (and_40_out, not_215_out, F13, not_216_out, not_217_out, not_218_out, OP4, not_219_out, not_220_out);
  and and_41 (and_41_out, F14, F13, not_221_out, OP6, OP5, OP4, not_222_out, not_223_out);
  and and_42 (and_42_out, not_224_out, OP5, OP4, not_225_out, OP2);
  and and_43 (and_43_out, F14, F13, F12, OP6, OP5, not_226_out, not_227_out, not_228_out);
  or or_1 (S0, and_1_out, and_2_out, and_3_out, and_4_out, and_5_out, and_6_out, and_7_out, and_8_out, and_9_out, and_10_out, and_11_out, and_12_out, and_13_out, and_14_out, and_15_out);
  or or_2 (S1, and_16_out, and_17_out, and_18_out, and_19_out, and_20_out, and_21_out, and_22_out, and_23_out);
  or or_3 (S2, and_24_out, and_25_out, and_26_out, and_27_out, and_28_out, and_29_out, and_30_out, and_31_out, and_32_out, and_33_out, and_34_out);
  or or_4 (S3, and_35_out, and_36_out, and_37_out, and_38_out, and_39_out, and_40_out, and_41_out, and_42_out, and_43_out);
endmodule

// 控制信号生成
module \控制信号自动生成  (
  input  OP2,
  input  OP3,
  input  OP4,
  input  OP5,
  input  OP6,
  input  F12,
  input  F13,
  input  F14,
  input  F25,
  input  F30,
  output MemToReg,
  output MemWrite,
  output ALU_SRC,
  output RegWrite,
  output ecall,
  output S_Type,
  output BEQ,
  output BNE,
  output JAL,
  output JALR,
  output CSRRSI,
  output CSRRCI
);

  wire and_1_out, and_2_out, and_4_out, and_5_out, and_6_out, and_7_out, and_8_out, and_9_out, and_10_out,
       and_11_out, and_12_out, and_13_out, and_14_out, and_15_out, and_16_out, and_17_out, and_18_out,
       and_19_out, and_20_out, and_21_out, and_22_out, and_23_out, and_24_out, and_25_out, and_26_out,
       and_27_out, and_28_out, and_29_out, and_30_out, and_31_out, and_32_out, and_33_out, and_34_out,
       and_35_out, and_36_out, and_39_out, and_40_out, not_1_out, not_2_out, not_3_out, not_4_out, not_5_out,
       not_6_out, not_7_out, not_8_out, not_9_out, not_10_out, not_11_out, not_12_out, not_13_out,
       not_14_out, not_15_out, not_16_out, not_17_out, not_18_out, not_19_out, not_20_out, not_21_out,
       not_22_out, not_23_out, not_24_out, not_25_out, not_26_out, not_27_out, not_28_out, not_29_out,
       not_30_out, not_31_out, not_32_out, not_33_out, not_34_out, not_35_out, not_36_out, not_37_out,
       not_38_out, not_39_out, not_40_out, not_41_out, not_42_out, not_43_out, not_44_out, not_45_out,
       not_46_out, not_47_out, not_48_out, not_49_out, not_50_out, not_51_out, not_52_out, not_53_out,
       not_54_out, not_55_out, not_56_out, not_57_out, not_58_out, not_59_out, not_60_out, not_61_out,
       not_62_out, not_63_out, not_64_out, not_65_out, not_66_out, not_67_out, not_68_out, not_69_out,
       not_70_out, not_71_out, not_72_out, not_73_out, not_74_out, not_75_out, not_76_out, not_77_out,
       not_78_out, not_79_out, not_80_out, not_81_out, not_82_out, not_83_out, not_84_out, not_85_out,
       not_86_out, not_87_out, not_88_out, not_89_out, not_90_out, not_91_out, not_92_out, not_93_out,
       not_94_out, not_95_out, not_96_out, not_97_out, not_98_out, not_99_out, not_100_out, not_101_out,
       not_102_out, not_103_out, not_104_out, not_105_out, not_106_out, not_107_out, not_108_out,
       not_109_out, not_110_out, not_111_out, not_112_out, not_113_out, not_114_out, not_115_out,
       not_116_out, not_117_out, not_118_out, not_119_out, not_120_out, not_121_out, not_122_out,
       not_123_out, not_124_out, not_125_out, not_126_out, not_127_out, not_128_out, not_129_out,
       not_130_out, not_131_out, not_132_out, not_133_out, not_134_out, not_135_out, not_136_out,
       not_137_out, not_138_out, not_139_out, not_140_out, not_141_out, not_142_out, not_143_out,
       not_144_out, not_145_out, not_146_out, not_147_out, not_148_out, not_149_out, not_150_out,
       not_151_out, not_152_out, not_153_out, not_154_out, not_155_out, not_156_out, not_157_out,
       not_158_out, not_159_out, not_160_out, not_161_out, not_162_out, not_163_out, not_164_out,
       not_165_out, not_166_out, not_167_out, not_168_out, not_169_out, not_170_out, not_171_out,
       not_172_out, not_173_out, not_174_out, not_175_out, not_176_out, not_177_out, not_178_out,
       not_179_out, not_180_out, not_181_out, not_182_out, not_183_out, not_184_out, not_185_out,
       not_186_out, not_187_out, not_188_out, not_189_out, not_190_out, not_191_out, not_192_out,
       not_193_out, not_194_out, not_195_out, not_196_out, not_197_out, not_198_out, not_199_out,
       not_200_out, not_201_out, not_202_out, not_203_out, not_204_out, not_205_out, not_206_out,
       not_207_out, not_208_out, not_209_out, not_210_out, not_211_out, not_212_out, not_213_out,
       not_214_out, not_215_out, not_216_out, not_217_out, not_218_out, not_219_out, not_220_out,
       not_221_out, not_222_out, not_223_out, not_224_out, not_225_out, not_226_out, not_227_out,
       not_228_out, not_229_out, not_230_out, not_231_out, not_232_out, not_233_out, not_234_out,
       not_235_out, not_236_out, not_237_out, not_238_out, not_239_out, not_240_out, not_241_out,
       not_242_out, not_243_out, not_244_out, not_245_out, not_246_out, not_247_out;

  not not_1 (not_1_out, F14);
  not not_2 (not_2_out, F12);
  not not_3 (not_3_out, OP6);
  not not_4 (not_4_out, OP5);
  not not_5 (not_5_out, OP4);
  not not_6 (not_6_out, OP3);
  not not_7 (not_7_out, OP2);
  not not_8 (not_8_out, F13);
  not not_9 (not_9_out, OP6);
  not not_10 (not_10_out, OP5);
  not not_11 (not_11_out, OP4);
  not not_12 (not_12_out, OP3);
  not not_13 (not_13_out, OP2);
  not not_14 (not_14_out, F14);
  not not_15 (not_15_out, F12);
  not not_16 (not_16_out, OP6);
  not not_17 (not_17_out, OP4);
  not not_18 (not_18_out, OP3);
  not not_19 (not_19_out, OP2);
  not not_20 (not_20_out, F14);
  not not_21 (not_21_out, F13);
  not not_22 (not_22_out, F12);
  not not_23 (not_23_out, OP6);
  not not_24 (not_24_out, OP5);
  not not_25 (not_25_out, OP3);
  not not_26 (not_26_out, OP2);
  not not_27 (not_27_out, OP6);
  not not_28 (not_28_out, OP5);
  not not_29 (not_29_out, OP3);
  not not_30 (not_30_out, OP2);
  not not_31 (not_31_out, F12);
  not not_32 (not_32_out, OP6);
  not not_33 (not_33_out, OP5);
  not not_34 (not_34_out, OP3);
  not not_35 (not_35_out, OP2);
  not not_36 (not_36_out, F13);
  not not_37 (not_37_out, F12);
  not not_38 (not_38_out, OP6);
  not not_39 (not_39_out, OP5);
  not not_40 (not_40_out, OP3);
  not not_41 (not_41_out, OP2);
  not not_42 (not_42_out, F14);
  not not_43 (not_43_out, F12);
  not not_44 (not_44_out, OP6);
  not not_45 (not_45_out, OP5);
  not not_46 (not_46_out, OP3);
  not not_47 (not_47_out, OP2);
  not not_48 (not_48_out, F30);
  not not_49 (not_49_out, F25);
  not not_50 (not_50_out, F14);
  not not_51 (not_51_out, F13);
  not not_52 (not_52_out, OP6);
  not not_53 (not_53_out, OP5);
  not not_54 (not_54_out, OP3);
  not not_55 (not_55_out, OP2);
  not not_56 (not_56_out, F30);
  not not_57 (not_57_out, F25);
  not not_58 (not_58_out, F13);
  not not_59 (not_59_out, OP6);
  not not_60 (not_60_out, OP5);
  not not_61 (not_61_out, OP3);
  not not_62 (not_62_out, OP2);
  not not_63 (not_63_out, F25);
  not not_64 (not_64_out, F13);
  not not_65 (not_65_out, OP6);
  not not_66 (not_66_out, OP5);
  not not_67 (not_67_out, OP3);
  not not_68 (not_68_out, OP2);
  not not_69 (not_69_out, F14);
  not not_70 (not_70_out, F12);
  not not_71 (not_71_out, OP6);
  not not_72 (not_72_out, OP5);
  not not_73 (not_73_out, OP4);
  not not_74 (not_74_out, OP3);
  not not_75 (not_75_out, OP2);
  not not_76 (not_76_out, F14);
  not not_77 (not_77_out, F12);
  not not_78 (not_78_out, OP6);
  not not_79 (not_79_out, OP4);
  not not_80 (not_80_out, OP3);
  not not_81 (not_81_out, OP2);
  not not_82 (not_82_out, F14);
  not not_83 (not_83_out, F13);
  not not_84 (not_84_out, F12);
  not not_85 (not_85_out, OP4);
  not not_86 (not_86_out, OP3);
  not not_87 (not_87_out, F13);
  not not_88 (not_88_out, OP6);
  not not_89 (not_89_out, OP5);
  not not_90 (not_90_out, OP4);
  not not_91 (not_91_out, OP3);
  not not_92 (not_92_out, OP2);
  not not_93 (not_93_out, OP4);
  not not_94 (not_94_out, OP3);
  not not_95 (not_95_out, OP2);
  not not_96 (not_96_out, F30);
  not not_97 (not_97_out, F25);
  not not_98 (not_98_out, F14);
  not not_99 (not_99_out, F13);
  not not_100 (not_100_out, F12);
  not not_101 (not_101_out, OP6);
  not not_102 (not_102_out, OP3);
  not not_103 (not_103_out, OP2);
  not not_104 (not_104_out, F25);
  not not_105 (not_105_out, F14);
  not not_106 (not_106_out, F13);
  not not_107 (not_107_out, F12);
  not not_108 (not_108_out, OP6);
  not not_109 (not_109_out, OP3);
  not not_110 (not_110_out, OP2);
  not not_111 (not_111_out, F30);
  not not_112 (not_112_out, F25);
  not not_113 (not_113_out, OP6);
  not not_114 (not_114_out, OP3);
  not not_115 (not_115_out, OP2);
  not not_116 (not_116_out, F30);
  not not_117 (not_117_out, F25);
  not not_118 (not_118_out, F12);
  not not_119 (not_119_out, OP6);
  not not_120 (not_120_out, OP3);
  not not_121 (not_121_out, OP2);
  not not_122 (not_122_out, F30);
  not not_123 (not_123_out, F25);
  not not_124 (not_124_out, F14);
  not not_125 (not_125_out, F12);
  not not_126 (not_126_out, OP6);
  not not_127 (not_127_out, OP3);
  not not_128 (not_128_out, OP2);
  not not_129 (not_129_out, F30);
  not not_130 (not_130_out, F25);
  not not_131 (not_131_out, F14);
  not not_132 (not_132_out, OP6);
  not not_133 (not_133_out, OP3);
  not not_134 (not_134_out, OP2);
  not not_135 (not_135_out, F14);
  not not_136 (not_136_out, F13);
  not not_137 (not_137_out, F12);
  not not_138 (not_138_out, OP6);
  not not_139 (not_139_out, OP5);
  not not_140 (not_140_out, OP3);
  not not_141 (not_141_out, OP2);
  not not_142 (not_142_out, OP6);
  not not_143 (not_143_out, OP5);
  not not_144 (not_144_out, OP3);
  not not_145 (not_145_out, OP2);
  not not_146 (not_146_out, F12);
  not not_147 (not_147_out, OP6);
  not not_148 (not_148_out, OP5);
  not not_149 (not_149_out, OP3);
  not not_150 (not_150_out, OP2);
  not not_151 (not_151_out, F13);
  not not_152 (not_152_out, F12);
  not not_153 (not_153_out, OP6);
  not not_154 (not_154_out, OP5);
  not not_155 (not_155_out, OP3);
  not not_156 (not_156_out, OP2);
  not not_157 (not_157_out, F14);
  not not_158 (not_158_out, F12);
  not not_159 (not_159_out, OP6);
  not not_160 (not_160_out, OP5);
  not not_161 (not_161_out, OP3);
  not not_162 (not_162_out, OP2);
  not not_163 (not_163_out, F30);
  not not_164 (not_164_out, F25);
  not not_165 (not_165_out, F14);
  not not_166 (not_166_out, F13);
  not not_167 (not_167_out, OP6);
  not not_168 (not_168_out, OP5);
  not not_169 (not_169_out, OP3);
  not not_170 (not_170_out, OP2);
  not not_171 (not_171_out, F30);
  not not_172 (not_172_out, F25);
  not not_173 (not_173_out, F13);
  not not_174 (not_174_out, OP6);
  not not_175 (not_175_out, OP5);
  not not_176 (not_176_out, OP3);
  not not_177 (not_177_out, OP2);
  not not_178 (not_178_out, F25);
  not not_179 (not_179_out, F13);
  not not_180 (not_180_out, OP6);
  not not_181 (not_181_out, OP5);
  not not_182 (not_182_out, OP3);
  not not_183 (not_183_out, OP2);
  not not_184 (not_184_out, F14);
  not not_185 (not_185_out, F12);
  not not_186 (not_186_out, OP6);
  not not_187 (not_187_out, OP5);
  not not_188 (not_188_out, OP4);
  not not_189 (not_189_out, OP3);
  not not_190 (not_190_out, OP2);
  not not_191 (not_191_out, OP4);
  not not_192 (not_192_out, F14);
  not not_193 (not_193_out, F13);
  not not_194 (not_194_out, F12);
  not not_195 (not_195_out, OP4);
  not not_196 (not_196_out, OP3);
  not not_197 (not_197_out, F25);
  not not_198 (not_198_out, F13);
  not not_199 (not_199_out, OP6);
  not not_200 (not_200_out, OP3);
  not not_201 (not_201_out, OP2);
  not not_202 (not_202_out, OP6);
  not not_203 (not_203_out, OP3);
  not not_204 (not_204_out, F13);
  not not_205 (not_205_out, OP6);
  not not_206 (not_206_out, OP5);
  not not_207 (not_207_out, OP4);
  not not_208 (not_208_out, OP3);
  not not_209 (not_209_out, OP2);
  not not_210 (not_210_out, F30);
  not not_211 (not_211_out, F25);
  not not_212 (not_212_out, F14);
  not not_213 (not_213_out, F13);
  not not_214 (not_214_out, F12);
  not not_215 (not_215_out, OP3);
  not not_216 (not_216_out, OP2);
  not not_217 (not_217_out, F14);
  not not_218 (not_218_out, F12);
  not not_219 (not_219_out, OP6);
  not not_220 (not_220_out, OP4);
  not not_221 (not_221_out, OP3);
  not not_222 (not_222_out, OP2);
  not not_223 (not_223_out, F14);
  not not_224 (not_224_out, F13);
  not not_225 (not_225_out, F12);
  not not_226 (not_226_out, OP4);
  not not_227 (not_227_out, OP3);
  not not_228 (not_228_out, OP2);
  not not_229 (not_229_out, OP4);
  not not_230 (not_230_out, OP3);
  not not_231 (not_231_out, OP2);
  not not_232 (not_232_out, F14);
  not not_233 (not_233_out, F13);
  not not_234 (not_234_out, OP4);
  not not_235 (not_235_out, OP3);
  not not_236 (not_236_out, OP2);
  not not_237 (not_237_out, OP4);
  not not_238 (not_238_out, F14);
  not not_239 (not_239_out, F13);
  not not_240 (not_240_out, F12);
  not not_241 (not_241_out, OP4);
  not not_242 (not_242_out, OP3);
  not not_243 (not_243_out, F12);
  not not_244 (not_244_out, OP3);
  not not_245 (not_245_out, OP2);
  not not_246 (not_246_out, OP3);
  not not_247 (not_247_out, OP2);
  and and_1 (and_1_out, not_1_out, F13, not_2_out, not_3_out, not_4_out, not_5_out, not_6_out, not_7_out);
  and and_2 (and_2_out, F14, not_8_out, F12, not_9_out, not_10_out, not_11_out, not_12_out, not_13_out);
  and and_3 (MemWrite, not_14_out, F13, not_15_out, not_16_out, OP5, not_17_out, not_18_out, not_19_out);
  and and_4 (and_4_out, not_20_out, not_21_out, not_22_out, not_23_out, not_24_out, OP4, not_25_out, not_26_out);
  and and_5 (and_5_out, F14, F13, F12, not_27_out, not_28_out, OP4, not_29_out, not_30_out);
  and and_6 (and_6_out, F14, F13, not_31_out, not_32_out, not_33_out, OP4, not_34_out, not_35_out);
  and and_7 (and_7_out, F14, not_36_out, not_37_out, not_38_out, not_39_out, OP4, not_40_out, not_41_out);
  and and_8 (and_8_out, not_42_out, F13, not_43_out, not_44_out, not_45_out, OP4, not_46_out, not_47_out);
  and and_9 (and_9_out, not_48_out, not_49_out, not_50_out, not_51_out, F12, not_52_out, not_53_out, OP4, not_54_out, not_55_out);
  and and_10 (and_10_out, not_56_out, not_57_out, F14, not_58_out, F12, not_59_out, not_60_out, OP4, not_61_out, not_62_out);
  and and_11 (and_11_out, F30, not_63_out, F14, not_64_out, F12, not_65_out, not_66_out, OP4, not_67_out, not_68_out);
  and and_12 (and_12_out, not_69_out, F13, not_70_out, not_71_out, not_72_out, not_73_out, not_74_out, not_75_out);
  and and_13 (and_13_out, not_76_out, F13, not_77_out, not_78_out, OP5, not_79_out, not_80_out, not_81_out);
  and and_14 (and_14_out, not_82_out, not_83_out, not_84_out, OP6, OP5, not_85_out, not_86_out, OP2);
  and and_15 (and_15_out, F14, not_87_out, F12, not_88_out, not_89_out, not_90_out, not_91_out, not_92_out);
  and and_16 (and_16_out, F14, F13, F12, OP6, OP5, not_93_out, not_94_out, not_95_out);
  and and_17 (and_17_out, not_96_out, not_97_out, not_98_out, not_99_out, not_100_out, not_101_out, OP5, OP4, not_102_out, not_103_out);
  and and_18 (and_18_out, F30, not_104_out, not_105_out, not_106_out, not_107_out, not_108_out, OP5, OP4, not_109_out, not_110_out);
  and and_19 (and_19_out, not_111_out, not_112_out, F14, F13, F12, not_113_out, OP5, OP4, not_114_out, not_115_out);
  and and_20 (and_20_out, not_116_out, not_117_out, F14, F13, not_118_out, not_119_out, OP5, OP4, not_120_out, not_121_out);
  and and_21 (and_21_out, not_122_out, not_123_out, not_124_out, F13, not_125_out, not_126_out, OP5, OP4, not_127_out, not_128_out);
  and and_22 (and_22_out, not_129_out, not_130_out, not_131_out, F13, F12, not_132_out, OP5, OP4, not_133_out, not_134_out);
  and and_23 (and_23_out, not_135_out, not_136_out, not_137_out, not_138_out, not_139_out, OP4, not_140_out, not_141_out);
  and and_24 (and_24_out, F14, F13, F12, not_142_out, not_143_out, OP4, not_144_out, not_145_out);
  and and_25 (and_25_out, F14, F13, not_146_out, not_147_out, not_148_out, OP4, not_149_out, not_150_out);
  and and_26 (and_26_out, F14, not_151_out, not_152_out, not_153_out, not_154_out, OP4, not_155_out, not_156_out);
  and and_27 (and_27_out, not_157_out, F13, not_158_out, not_159_out, not_160_out, OP4, not_161_out, not_162_out);
  and and_28 (and_28_out, not_163_out, not_164_out, not_165_out, not_166_out, F12, not_167_out, not_168_out, OP4, not_169_out, not_170_out);
  and and_29 (and_29_out, not_171_out, not_172_out, F14, not_173_out, F12, not_174_out, not_175_out, OP4, not_176_out, not_177_out);
  and and_30 (and_30_out, F30, not_178_out, F14, not_179_out, F12, not_180_out, not_181_out, OP4, not_182_out, not_183_out);
  and and_31 (and_31_out, not_184_out, F13, not_185_out, not_186_out, not_187_out, not_188_out, not_189_out, not_190_out);
  and and_32 (and_32_out, OP6, OP5, not_191_out, OP3, OP2);
  and and_33 (and_33_out, not_192_out, not_193_out, not_194_out, OP6, OP5, not_195_out, not_196_out, OP2);
  and and_34 (and_34_out, F30, not_197_out, F14, not_198_out, F12, not_199_out, OP5, OP4, not_200_out, not_201_out);
  and and_35 (and_35_out, not_202_out, OP5, OP4, not_203_out, OP2);
  and and_36 (and_36_out, F14, not_204_out, F12, not_205_out, not_206_out, not_207_out, not_208_out, not_209_out);
  and and_37 (ecall, not_210_out, not_211_out, not_212_out, not_213_out, not_214_out, OP6, OP5, OP4, not_215_out, not_216_out);
  and and_38 (S_Type, not_217_out, F13, not_218_out, not_219_out, OP5, not_220_out, not_221_out, not_222_out);
  and and_39 (and_39_out, not_223_out, not_224_out, not_225_out, OP6, OP5, not_226_out, not_227_out, not_228_out);
  and and_40 (and_40_out, F14, F13, F12, OP6, OP5, not_229_out, not_230_out, not_231_out);
  and and_41 (BNE, not_232_out, not_233_out, F12, OP6, OP5, not_234_out, not_235_out, not_236_out);
  and and_42 (JAL, OP6, OP5, not_237_out, OP3, OP2);
  and and_43 (JALR, not_238_out, not_239_out, not_240_out, OP6, OP5, not_241_out, not_242_out, OP2);
  and and_44 (CSRRSI, F14, F13, not_243_out, OP6, OP5, OP4, not_244_out, not_245_out);
  and and_45 (CSRRCI, F14, F13, F12, OP6, OP5, OP4, not_246_out, not_247_out);
  or or_1 (MemToReg, and_1_out, and_2_out);
  or or_2 (BEQ, and_39_out, and_40_out);
  or or_3 (ALU_SRC, and_4_out, and_5_out, and_6_out, and_7_out, and_8_out, and_9_out, and_10_out, and_11_out, and_12_out, and_13_out, and_14_out, and_15_out, and_16_out);
  or or_4 (RegWrite, and_17_out, and_18_out, and_19_out, and_20_out, and_21_out, and_22_out, and_23_out, and_24_out, and_25_out, and_26_out, and_27_out, and_28_out, and_29_out, and_30_out, and_31_out, and_32_out, and_33_out, and_34_out, and_35_out, and_36_out);
endmodule

// ALU
module ALU (
  input  [31:0] X,
  input  [31:0] Y,
  input  [3:0] AluOP,
  output out_4,
  output Equal,
  output out_6,
  output [31:0] Result,
  output [31:0] Result_2
);

  wire [0:0] comparator_1_lt, comparator_2_lt;
  wire [31:0] adder_1_out, AND_out, divider_1_out, divider_1_rem, multiplier_1_cout, multiplier_1_out,
       NOR_out, OR_out, shifter_1_out, shifter_2_out, shifter_3_out, subtractor_1_out, XOR_out;

  assign AND_out = X & Y;  // AND_Gate AND, 32 bits wide
  assign OR_out = X | Y;  // OR_Gate OR, 32 bits wide
  Shifter #(.width(32), .shift("ll")) shifter_1 (.in(X), .\dist (Y[4:0]), .out(shifter_1_out));
  Shifter #(.width(32), .shift("ar")) shifter_2 (.in(X), .\dist (Y[4:0]), .out(shifter_2_out));
  Shifter #(.width(32), .shift("lr")) shifter_3 (.in(X), .\dist (Y[4:0]), .out(shifter_3_out));
  Multiplier #(.width(32)) multiplier_1 (.a(X), .b(Y), .out(multiplier_1_out), .cout(multiplier_1_cout));  // open: cin
  Divider #(.width(32)) divider_1 (.a(X), .b(Y), .out(divider_1_out), .rem(divider_1_rem));  // open: upper
  Adder #(.width(32)) adder_1 (.a(X), .b(Y), .out(adder_1_out));  // open: cin, cout
  Subtractor #(.width(32)) subtractor_1 (.a(X), .b(Y), .out(subtractor_1_out));  // open: bin, bout
  assign XOR_out = X ^ Y;  // XOR_Gate XOR, 32 bits wide
  assign NOR_out = ~(X | Y);  // NOR_Gate NOR, 32 bits wide
  Comparator #(.width(32), .mode("twosComplement")) comparator_1 (
    .a(X), .b(Y), .eq(Equal), .lt(comparator_1_lt[0]));  // open: gt
  Comparator #(.width(32), .mode("unsigned")) comparator_2 (.a(X), .b(Y), .lt(comparator_2_lt[0]));  // open: gt, eq
  Multiplexer #(.select(4), .width(32), .disabled("Z"), .enable("false")) multiplexer_1 (
    .in0(shifter_1_out), .in1(shifter_2_out), .in2(shifter_3_out), .in3(multiplier_1_out),
    .in4(divider_1_out), .in5(adder_1_out), .in6(subtractor_1_out), .in7(AND_out), .in8(OR_out),
    .in9(XOR_out), .in10(NOR_out), .in11({{31{1'b0}}, comparator_1_lt[0]}),
    .in12({{31{1'b0}}, comparator_2_lt[0]}), .in13({32{1'b0}}), .in14({32{1'b0}}), .in15({32{1'b0}}),
    .out(Result), .sel(AluOP));
  Multiplexer #(.select(4), .width(32), .disabled("Z"), .enable("false")) multiplexer_2 (
    .in0({32{1'b0}}), .in1({32{1'b0}}), .in2({32{1'b0}}), .in3(multiplier_1_cout), .in4(divider_1_rem),
    .in5({32{1'b0}}), .in6({32{1'b0}}), .in7({32{1'b0}}), .in8({32{1'b0}}), .in9({32{1'b0}}),
    .in10({32{1'b0}}), .in11({32{1'b0}}), .in12({32{1'b0}}), .in13({32{1'b0}}), .in14({32{1'b0}}),
    .in15({32{1'b0}}), .out(Result_2), .sel(AluOP));
  Multiplexer #(.select(4), .width(1), .disabled("Z"), .enable("false")) multiplexer_3 (
    .in0(1'b0), .in1(1'b0), .in2(1'b0), .in3(1'b0), .in4(1'b0), .in5(1'b0), .in6(1'b0), .in7(1'b0),
    .in8(1'b0), .in9(1'b0), .in10(1'b0), .in11(comparator_1_lt[0]), .in12(comparator_2_lt[0]), .in13(1'b0),
    .in14(1'b0), .in15(1'b0), .out(out_6), .sel(AluOP));
  not not_1 (out_4, out_6);

  // Other names for the same wires on the sheet: Result2[31:0] = Result_2; S[3:0] = AluOP; tunnel = out_6;
  //   tunnel_t = out_4

  // Notes on the sheet:
  //   不要改变此引脚区域内容，也不要改变ALU封装形式
  //   输入引脚
  //   输出引脚
endmodule

module Regifile (
  input  [31:0] Din,
  input  Clk,
  input  WE,
  input  [4:0] R1_num,
  input  [4:0] W_num,
  input  [4:0] R2_num,
  output [31:0] R1,
  output [31:0] R2
);

  // RegisterFile registerfile_1: pin names not known; wires that end beside it: Din, Clk, WE, W_num, R1_num, R2_num, R1, R2
endmodule

module \中断按键参考电路  (
  input  \同步清零信号 ,
  output \与中断屏蔽位与 
);

  wire \_1号中断_out , and_1_out, clock_1_out, d_ff_1_q, or_1_out, or_2_out;

  Clock #(.highDuration(1), .lowDuration(1)) clock_1 (.out(clock_1_out));
  Button \_1号中断  (.out(\_1号中断_out ));
  LED #(.active("true")) \_1号中断等待指示灯  (.in(or_1_out));
  or or_1 (or_1_out, \与中断屏蔽位与 , d_ff_1_q);
  D_Flip_Flop #(.trigger("rising"), .Pre_Clr_Positions("LEGACY"), .NegatePresetClear("false"), .enable("true"), .NewFFLayout("false")) d_ff_1 (
    .clk(\_1号中断_out ), .D(1'b1), .Q(d_ff_1_q), .reset(\与中断屏蔽位与 ));  // open: Qn, preset, en
  or or_2 (or_2_out, d_ff_1_q, \与中断屏蔽位与 );
  and and_1 (and_1_out, or_2_out, ~\同步清零信号 );  // AND_Gate
  D_Flip_Flop #(.trigger("rising"), .Pre_Clr_Positions("LEGACY"), .NegatePresetClear("false"), .enable("true"), .NewFFLayout("false")) IR1 (
    .clk(clock_1_out), .D(and_1_out), .Q(\与中断屏蔽位与 ));  // open: Qn, preset, en, reset

  // Notes on the sheet:
  //   中断信号采样参考电路
  //   Reset 
endmodule
module \单周期_单级中断  (
  input  IR1,
  input  IR2,
  input  IR3,
  output RegWrite,
  output MemWrite,
  output [31:0] PC,
  output [31:0] IR,
  output [31:0] RDin,
  output [31:0] MDin,
  output [31:0] LedData
);

  wire ALUeq, ALUge, ALUle, and_1_out, and_2_out, and_3_out, and_4_out, and_6_out, and_7_out, and_8_out,
       and_9_out, and_10_out, Beq, BGEU, Bne, Btype, CLK, clock_1_out, CLR1, CLR2, CLR3, comparator_1_eq,
       comparator_2_eq, comparator_3_eq, comparator_4_eq, comparator_5_eq, comparator_5_lt, comparator_6_eq,
       comparator_6_gt, comparator_6_lt, comparator_7_eq, d_ff_1_q, d_ff_2_q, d_ff_3_q, d_ff_4_q, ecall, Go,
       halt, halt_1, IE, INTR, INTR1, INTR2, INTR3, IR1_t, IR2_t, IR3_t, IRA, IRB, IRC, IRHAVE, JAL, JALR,
       Jtype, LHU, LUI, MemToReg, nand_1_out, not_1_out, not_2_out, not_3_out, or_1_out, or_7_out, or_9_out,
       or_12_out, or_13_out, or_14_out, or_16_out, or_17_out, RST, SRA, Stype, URET, W1, W2, W3,
       \单周期硬布线控制器_1_p17 ;
  wire [1:0] priority_encoder_1_out, priority_encoder_2_out, priority_encoder_3_out, register_1_q;
  wire [3:0] \单周期硬布线控制器_1_p16 ;
  wire [4:0] multiplexer_4_out, multiplexer_5_out;
  wire [12:0] CNT_num;
  wire [15:0] multiplexer_9_out, \总周期数 ;
  wire [31:0] ALUres, bit_extender_1_out, bit_extender_2_out, bit_extender_3_out, bit_extender_4_out,
       bit_extender_5_out, bit_extender_6_out, Dout, IR_PC, MEPC, multiplexer_2_out, multiplexer_3_out,
       multiplexer_6_out, multiplexer_7_out, multiplexer_8_out, multiplexer_10_out, PC_4, PC_B, PC_J,
       regifile_1_r1, shifter_1_out, shifter_2_out, shifter_3_out;

  Button \u_继续运行  (.out(Go));
  Button _1 (.out(IRA));
  Button _2 (.out(IRB));
  Button _3 (.out(IRC));
  LED #(.active("true")) led_1 (.in(W1));
  LED #(.active("true")) led_2 (.in(W2));
  LED #(.active("true")) led_3 (.in(W3));
  Hex_Digit_Display hex_digit_display_1 (.value(LedData[31:28]));  // open: dp
  Comparator #(.width(16), .mode("twosComplement")) comparator_1 (
    .a(16'h23b), .b(\总周期数 ), .eq(comparator_1_eq));  // open: gt, lt
  Comparator #(.width(16), .mode("twosComplement")) comparator_2 (
    .a(\总周期数 ), .b(16'h1), .eq(comparator_2_eq));  // open: gt, lt
  Comparator #(.width(16), .mode("twosComplement")) comparator_3 (
    .a(\总周期数 ), .b(16'h4), .eq(comparator_3_eq));  // open: gt, lt
  Comparator #(.width(16), .mode("twosComplement")) comparator_4 (
    .a(\总周期数 ), .b(16'h7), .eq(comparator_4_eq));  // open: gt, lt
  not not_1 (not_1_out, ALUeq);
  Hex_Digit_Display hex_digit_display_2 (.value(LedData[27:24]));  // open: dp
  Hex_Digit_Display hex_digit_display_3 (.value(LedData[23:20]));  // open: dp
  or or_1 (or_1_out, comparator_1_eq, comparator_2_eq);
  assign IRA = or_1_out ? ~CLK : 1'bz;  // Controlled_Inverter controlled_inverter_1
  assign IRB = comparator_3_eq ? ~CLK : 1'bz;  // Controlled_Inverter controlled_inverter_2
  assign IRC = comparator_4_eq ? ~CLK : 1'bz;  // Controlled_Inverter controlled_inverter_3
  and and_1 (and_1_out, Beq, ALUeq);
  and and_2 (and_2_out, not_1_out, Bne);
  and and_3 (and_3_out, BGEU, ALUge);
  Multiplexer #(.select(2), .width(32), .disabled("Z"), .enable("false")) multiplexer_1 (
    .in0(32'h30ac), .in1(32'h3150), .in2(32'h31f4), .out(IR_PC), .sel(priority_encoder_1_out));  // open: in3
  Priority_Encoder #(.select(2), .disabled("Z")) priority_encoder_1 (
    .in0(INTR1), .in1(INTR2), .in2(INTR3), .out(priority_encoder_1_out));  // open: in3, gs, en_out, en_in
  Hex_Digit_Display hex_digit_display_4 (.value(LedData[19:16]));  // open: dp
  Hex_Digit_Display hex_digit_display_5 (.value(LedData[15:12]));  // open: dp
  Pull_Resistor #(.pull(0)) pull_resistor_1 (.node(IRA));
  Pull_Resistor #(.pull(0)) pull_resistor_2 (.node(IRB));
  Pull_Resistor #(.pull(0)) pull_resistor_3 (.node(IRC));
  or or_2 (Btype, and_1_out, and_2_out, and_3_out);
  Hex_Digit_Display hex_digit_display_6 (.value(LedData[11:8]));  // open: dp
  Hex_Digit_Display hex_digit_display_7 (.value(LedData[7:4]));  // open: dp
  // Probe on \总周期数 
  Hex_Digit_Display hex_digit_display_8 (.value(LedData[3:0]));  // open: dp
  Priority_Encoder #(.select(2), .disabled("Z")) priority_encoder_2 (
    .in0(1'b1), .in1(JALR), .in2(JAL), .in3(Btype), .out(priority_encoder_2_out));  // open: gs, en_out, en_in
  Multiplexer #(.select(2), .width(32), .disabled("Z"), .enable("false")) multiplexer_2 (
    .in0(PC_4), .in1(ALUres), .in2(PC_J), .in3(PC_B), .out(multiplexer_2_out), .sel(priority_encoder_2_out));
  or or_3 (W1, INTR1, d_ff_1_q);
  Register #(.width(2), .trigger("rising"), .Select("low")) register_1 (
    .D(priority_encoder_1_out), .en(INTR), .Q(register_1_q), .clk(CLK));  // open: clr
  Demultiplexer #(.select(2), .width(1), .tristate("false"), .disabled("Z"), .enable("false")) demultiplexer_1 (
    .out0(CLR1), .out1(CLR2), .out2(CLR3), .in(URET), .sel(register_1_q));  // open: out3
  or or_4 (IR1_t, IR1, IRA);
  D_Flip_Flop #(.trigger("rising"), .Pre_Clr_Positions("LEGACY"), .NegatePresetClear("false"), .enable("true"), .NewFFLayout("false")) d_ff_1 (
    .clk(IRA), .D(1'b1), .Q(d_ff_1_q), .reset(INTR1));  // open: Qn, preset, en
  or or_5 (IR2_t, IR2, IRB);
  or or_6 (IRHAVE, INTR1, INTR2, INTR3);
  Multiplexer #(.select(2), .width(32), .disabled("Z"), .enable("false")) multiplexer_3 (
    .in0(multiplexer_2_out), .in1(IR_PC), .in2(MEPC), .out(multiplexer_3_out), .sel(priority_encoder_3_out));  // open: in3
  Priority_Encoder #(.select(2), .disabled("Z")) priority_encoder_3 (
    .in0(1'b1), .in1(INTR), .in2(URET), .out(priority_encoder_3_out));  // open: in3, gs, en_out, en_in
  or or_7 (or_7_out, d_ff_1_q, INTR1);
  and and_4 (and_4_out, or_7_out, ~CLR1);  // AND_Gate
  Register #(.width(32), .trigger("rising"), .Select("low")) register_2 (
    .D(multiplexer_2_out), .en(INTR), .Q(MEPC), .clk(CLK));  // open: clr
  or or_8 (IR3_t, IR3, IRC);
  and and_5 (INTR, IE, IRHAVE);
  D_Flip_Flop #(.trigger("rising"), .Pre_Clr_Positions("LEGACY"), .NegatePresetClear("false"), .enable("true"), .NewFFLayout("false")) u_IR1 (
    .clk(CLK), .D(and_4_out), .Q(INTR1));  // open: Qn, preset, en, reset
  Register #(.width(32), .trigger("rising"), .Select("low")) u_PC (
    .D(multiplexer_3_out), .en(or_9_out), .Q(PC), .clk(CLK), .clr(RST));
  or or_9 (or_9_out, Go, not_2_out);
  not not_2 (not_2_out, halt);
  or or_10 (Jtype, JAL, JALR);
  // RiscV_Probe riscv_probe_1: pin names not known; wires that end beside it: IR
  Adder #(.width(32)) adder_1 (.a(PC), .b(32'h4), .out(PC_4));  // open: cin, cout
  or or_11 (W2, INTR2, d_ff_2_q);
  ROM #(.addrWidth(10), .dataWidth(32), .Select("high")) rom_1 (.addr(PC[11:2]), .data(IR));
  not not_3 (not_3_out, halt);
  D_Flip_Flop #(.trigger("rising"), .Pre_Clr_Positions("LEGACY"), .NegatePresetClear("false"), .enable("true"), .NewFFLayout("false")) d_ff_2 (
    .clk(IRB), .D(1'b1), .Q(d_ff_2_q), .reset(INTR2));  // open: Qn, preset, en
  or or_12 (or_12_out, Go, not_3_out);
  // 单周期硬布线控制器 单周期硬布线控制器_1: pin names not known; wires that end beside it: JAL, SRA, JALR, LUI, URET, IR[21], IR[6:2], {IR[30], IR[25], IR[14:12]}, LHU, ecall, BGEU, Beq, Bne, MemToReg, MemWrite, \单周期硬布线控制器_1_p16 , \单周期硬布线控制器_1_p17 , RegWrite, Stype
  Multiplexer #(.select(1), .width(5), .disabled("Z"), .enable("false")) multiplexer_4 (
    .in0(IR[19:15]), .in1(5'b10001), .out(multiplexer_4_out), .sel(ecall));
  Multiplexer #(.select(1), .width(5), .disabled("Z"), .enable("false")) multiplexer_5 (
    .in0(IR[24:20]), .in1(5'b01010), .out(multiplexer_5_out), .sel(ecall));
  Counter #(.width(16), .max('hffff), .ongoal("wrap"), .trigger("rising"), .behavior("new")) counter_1 (
    .count(or_12_out), .Q(\总周期数 ), .clk(CLK));  // open: load, D, carry, clr, preset, down
  or or_13 (or_13_out, d_ff_2_q, INTR2);
  and and_6 (and_6_out, or_13_out, ~CLR2);  // AND_Gate
  assign bit_extender_1_out = {{20{IR[31]}}, IR[31:20]};  // Bit_Extender bit_extender_1
  Multiplexer #(.select(1), .width(32), .disabled("Z"), .enable("false")) multiplexer_6 (
    .in0(bit_extender_1_out), .in1(bit_extender_2_out), .out(multiplexer_6_out), .sel(Stype));
  assign bit_extender_2_out = {{20{IR[31]}}, {IR[31:25], IR[11:7]}};  // Bit_Extender bit_extender_2
  assign bit_extender_3_out = {{20{IR[31]}}, {IR[31], IR[7], IR[30:25], IR[11:8]}};  // Bit_Extender bit_extender_3
  assign bit_extender_4_out = {{12{IR[31]}}, {IR[31], IR[19:12], IR[20], IR[30:21]}};  // Bit_Extender bit_extender_4
  D_Flip_Flop #(.trigger("high"), .Pre_Clr_Positions("LEGACY"), .NegatePresetClear("false"), .enable("true"), .NewFFLayout("false")) d_ff_3 (.Q(d_ff_3_q));  // open: clk, D, Qn, preset, en, reset
  // Probe on 13'hc
  D_Flip_Flop #(.trigger("rising"), .Pre_Clr_Positions("LEGACY"), .NegatePresetClear("false"), .enable("true"), .NewFFLayout("false")) u_IR2 (
    .clk(CLK), .D(and_6_out), .Q(INTR2));  // open: Qn, preset, en, reset
  Regifile regifile_1 (
    .Din(RDin), .Clk(CLK), .R1(regifile_1_r1), .R2(MDin), .WE(RegWrite), .W_num(IR[11:7]),
    .R1_num(multiplexer_4_out), .R2_num(multiplexer_5_out));
  Shifter #(.width(32), .shift("ll")) shifter_1 (.in(bit_extender_3_out), .\dist (5'b00001), .out(shifter_1_out));
  Shifter #(.width(32), .shift("ll")) shifter_2 (.in(bit_extender_4_out), .\dist (5'b00001), .out(shifter_2_out));
  Comparator #(.width(13), .mode("twosComplement")) comparator_5 (
    .a(CNT_num), .b(13'hc), .eq(comparator_5_eq), .lt(comparator_5_lt));  // open: gt
  Clock #(.highDuration(1), .lowDuration(1)) clock_1 (.out(clock_1_out));
  Multiplexer #(.select(1), .width(32), .disabled("Z"), .enable("false")) multiplexer_7 (
    .in0(MDin), .in1(multiplexer_6_out), .out(multiplexer_7_out), .sel(\单周期硬布线控制器_1_p17 ));
  Counter #(.width(13), .max('h1fff), .ongoal("stay"), .trigger("rising"), .behavior("old")) counter_2 (
    .count(comparator_5_lt), .Q(CNT_num), .clk(clock_1_out));  // open: load, D, carry, clr, preset
  Adder #(.width(32)) adder_2 (.a(shifter_1_out), .b(PC), .out(PC_B));  // open: cin, cout
  Adder #(.width(32)) adder_3 (.a(shifter_2_out), .b(PC), .out(PC_J));  // open: cin, cout
  nand nand_1 (nand_1_out, d_ff_3_q, comparator_5_eq);
  or or_14 (or_14_out, ~IRHAVE, URET);  // OR_Gate
  or or_15 (W3, INTR3, d_ff_4_q);
  Comparator #(.width(32), .mode("twosComplement")) comparator_6 (
    .a(32'h22), .b(regifile_1_r1), .gt(comparator_6_gt), .eq(comparator_6_eq), .lt(comparator_6_lt));
  ALU alu_1 (
    .X(regifile_1_r1), .Y(multiplexer_7_out), .AluOP(\单周期硬布线控制器_1_p16 ), .Equal(ALUeq), .Result(ALUres),
    .out_4(ALUge), .out_6(ALUle));  // open: Result_2
  assign CLK = nand_1_out ? clock_1_out : 1'bz;  // Controlled_Buffer controlled_buffer_1
  Pull_Resistor #(.pull(1)) pull_resistor_4 (.node(CLK));
  D_Flip_Flop #(.trigger("rising"), .Pre_Clr_Positions("LEGACY"), .NegatePresetClear("false"), .enable("true"), .NewFFLayout("false")) d_ff_4 (
    .clk(IRC), .D(1'b1), .Q(d_ff_4_q), .reset(INTR3));  // open: Qn, preset, en
  and and_7 (and_7_out, ecall, comparator_6_eq);
  D_Flip_Flop #(.trigger("rising"), .Pre_Clr_Positions("LEGACY"), .NegatePresetClear("false"), .enable("true"), .NewFFLayout("true")) d_ff_5 (
    .clk(CLK), .D(or_14_out), .Q(IE));  // open: Qn, preset, en, reset
  Register #(.width(32), .trigger("rising"), .Select("low")) register_3 (
    .D(MDin), .en(and_7_out), .Q(LedData), .clk(CLK));  // open: clr
  or or_16 (or_16_out, d_ff_4_q, INTR3);
  and and_8 (and_8_out, or_16_out, ~CLR3);  // AND_Gate
  and and_9 (and_9_out, or_17_out, ecall);
  or or_17 (or_17_out, comparator_6_gt, comparator_6_lt);
  Multiplexer #(.select(2), .width(32), .disabled("Z"), .enable("false")) multiplexer_8 (
    .in0(ALUres), .in1(Dout), .in2(PC_4), .in3(PC_4), .out(multiplexer_8_out), .sel({Jtype, MemToReg}));
  D_Flip_Flop #(.trigger("rising"), .Pre_Clr_Positions("LEGACY"), .NegatePresetClear("false"), .enable("true"), .NewFFLayout("false")) u_IR3 (
    .clk(CLK), .D(and_8_out), .Q(INTR3));  // open: Qn, preset, en, reset
  D_Flip_Flop #(.trigger("falling"), .Pre_Clr_Positions("ABOVE_BELOW"), .NegatePresetClear("false"), .enable("true"), .NewFFLayout("true")) d_ff_6 (
    .clk(CLK), .D(1'b1), .Q(halt_1), .en(and_9_out), .reset(Go));  // open: Qn, preset
  RAM #(.addrWidth(10), .dataWidth(32), .bus("separate"), .Select("high")) ram_1 (
    .addr(ALUres[11:2]), .din(MDin), .data(Dout), .str(MemWrite), .sel(1'b1), .clk(CLK), .ld(1'b1));  // open: clr
  Comparator #(.width(32), .mode("twosComplement")) comparator_7 (
    .a(32'h1), .b(LedData), .eq(comparator_7_eq));  // open: gt, lt
  and and_10 (and_10_out, BGEU, comparator_7_eq);
  Multiplexer #(.select(1), .width(16), .disabled("Z"), .enable("false")) multiplexer_9 (
    .in0(multiplexer_8_out[15:0]), .in1(multiplexer_8_out[31:16]), .out(multiplexer_9_out), .sel(ALUres[0]));
  or or_18 (halt, and_10_out, halt_1);
  assign bit_extender_5_out = {{16{1'b0}}, multiplexer_9_out};  // Bit_Extender bit_extender_5
  assign bit_extender_6_out = {{12{1'b0}}, IR[31:12]};  // Bit_Extender bit_extender_6
  Multiplexer #(.select(1), .width(32), .disabled("Z"), .enable("false")) multiplexer_10 (
    .in0(multiplexer_8_out), .in1(bit_extender_5_out), .out(multiplexer_10_out), .sel(LHU));
  Shifter #(.width(32), .shift("ll")) shifter_3 (.in(bit_extender_6_out), .\dist (5'b01100), .out(shifter_3_out));
  Multiplexer #(.select(1), .width(32), .disabled("Z"), .enable("false")) multiplexer_11 (
    .in0(multiplexer_10_out), .in1(shifter_3_out), .out(RDin), .sel(LUI));

  // Other names for the same wires on the sheet: Imm[19:0] = IR[31:12]

  // Notes on the sheet:
  //   中断源
  //   中断等待指示
  //   总复位信号应将除ROM以外所有存储组件全部清零
  //   单级中断测试信号模拟器
  //   数码管输出
  //   数码管输出应该用寄存器锁存，否则显示数据只能一闪而过
  //   中断响应阶段
  //   中断响应
  //   指令探针
  //   指令存储器
  //   为方便自动评测，需要输出PC，IR，寄存器堆写如数据RDin
  //   指令字
  //   contents of rom_1 (hex, n*v repeats v):
  //   7d000113 100413 1f41993 41f9d993 433 c00913 800b13 140413 f47413 800293 100313 499993 89e9b3 1300533
  //   2200893 73 406282b3 fe0294e3 140413 f00f93 1f47433 1c41413 800293 100313 49d993 89e9b3 1300533
  //   2200893 73 406282b3 fe0294e3 1c45413 406b0b33 b0463 f95ff06f 2b3 fff2c293 1029293 fff2e293 500533
  //   2200893 73 f5dff06f 1112023 410113 a12023 410113 812023 410113 1312023 410113 1412023 410113 1512023
  //   410113 1612023 410113 100b13 300a13 100a93 1600433 441413 14469b3 1300533 2200893 73 fe0416e3
  //   415a0a33 fe0a10e3 ffc10113 12b03 ffc10113 12a83 ffc10113 12a03 ffc10113 12983 ffc10113 12403
  //   ffc10113 12503 ffc10113 12883 200073 1112023 410113 a12023 410113 812023 410113 1312023 410113
  //   1412023 410113 1512023 410113 1612023 410113 200b13 300a13 100a93 1600433 441413 14469b3 1300533
  //   2200893 73 fe0416e3 415a0a33 fe0a10e3 ffc10113 12b03 ffc10113 12a83 ffc10113 12a03 ffc10113 12983
  //   ffc10113 12403 ffc10113 12503 ffc10113 12883 200073 1112023 410113 a12023 410113 812023 410113
  //   1312023 410113 1412023 410113 1512023 410113 1612023 410113 300b13 300a13 100a93 1600433 441413
  //   14469b3 1300533 2200893 73 fe0416e3 415a0a33 fe0a10e3 ffc10113 12b03 ffc10113 12a83 ffc10113 12a03
  //   ffc10113 12983 ffc10113 12403 ffc10113 12503 ffc10113 12883 200073
  //   RAM写使能MemWrite、RAM写入数据MDin等信号
  //   JALR
  //   URET
  //   Beq
  //   Bne
  //   MemToReg
  //   MemWrite
  //   AluOP
  //   AluSrcB
  //   RegWrite
  //   控制位
  //   暂停节拍，不能为0
  //   戳工具置1进入计数暂停模式，ctrl+k时钟自动运行到对应节拍暂停
  //   ctrl+k关闭时钟连续运行，将控制位置零，进入单步调试模式调试
  //   中断使能位(用于开关中断)
  //   判断中断使能
  //   可计数暂停的时钟源
  //   数据存储器
endmodule

module MapReg_1 (
  input  [31:0] Data,
  input  En,
  input  [9:0] Addr,
  input  CLK,
  input  RST,
  output [31:0] \行1 ,
  output [31:0] \行9 ,
  output [31:0] \行17 ,
  output [31:0] \行25 ,
  output [31:0] \行2 ,
  output [31:0] \行10 ,
  output [31:0] \行18 ,
  output [31:0] \行26 ,
  output [31:0] \行3 ,
  output [31:0] \行11 ,
  output [31:0] \行19 ,
  output [31:0] \行27 ,
  output [31:0] \行4 ,
  output [31:0] \行12 ,
  output [31:0] \行20 ,
  output [31:0] \行28 ,
  output [31:0] \行5 ,
  output [31:0] \行13 ,
  output [31:0] \行21 ,
  output [31:0] \行29 ,
  output [31:0] \行6 ,
  output [31:0] \行14 ,
  output [31:0] \行22 ,
  output [31:0] \行30 ,
  output [31:0] \行7 ,
  output [31:0] \行15 ,
  output [31:0] \行23 ,
  output [31:0] \行31 ,
  output [31:0] \行8 ,
  output [31:0] \行16 ,
  output [31:0] \行24 ,
  output [31:0] \行32 
);

  wire and_1_out, and_2_out, and_3_out, and_4_out, and_5_out, and_6_out, and_7_out, and_8_out, and_9_out,
       and_10_out, and_11_out, and_12_out, and_13_out, and_14_out, and_15_out, and_16_out, and_17_out,
       and_18_out, and_19_out, and_20_out, and_21_out, and_22_out, and_23_out, and_24_out, and_25_out,
       and_26_out, and_27_out, and_28_out, and_29_out, and_30_out, and_31_out, and_32_out, \行1_t , \行2_t ,
       \行3_t , \行4_t , \行5_t , \行6_t , \行7_t , \行8_t , \行9_t , \行10_t , \行11_t , \行12_t , \行13_t , \行14_t ,
       \行15_t , \行16_t , \行17_t , \行18_t , \行19_t , \行20_t , \行21_t , \行22_t , \行23_t , \行24_t , \行25_t ,
       \行26_t , \行27_t , \行28_t , \行29_t , \行30_t , \行31_t , \行32_t ;

  and and_1 (and_1_out, En, \行1_t );
  and and_2 (and_2_out, En, \行2_t );
  and and_3 (and_3_out, En, \行3_t );
  and and_4 (and_4_out, En, \行4_t );
  and and_5 (and_5_out, En, \行5_t );
  and and_6 (and_6_out, En, \行6_t );
  and and_7 (and_7_out, En, \行7_t );
  and and_8 (and_8_out, En, \行8_t );
  Register #(.width(32), .trigger("rising"), .Select("low")) register_1 (
    .D(Data), .en(and_1_out), .Q(\行1 ), .clk(CLK), .clr(RST));
  Register #(.width(32), .trigger("rising"), .Select("low")) register_2 (
    .D(Data), .en(and_2_out), .Q(\行2 ), .clk(CLK), .clr(RST));
  Register #(.width(32), .trigger("rising"), .Select("low")) register_3 (
    .D(Data), .en(and_3_out), .Q(\行3 ), .clk(CLK), .clr(RST));
  Register #(.width(32), .trigger("rising"), .Select("low")) register_4 (
    .D(Data), .en(and_4_out), .Q(\行4 ), .clk(CLK), .clr(RST));
  Register #(.width(32), .trigger("rising"), .Select("low")) register_5 (
    .D(Data), .en(and_5_out), .Q(\行5 ), .clk(CLK), .clr(RST));
  Register #(.width(32), .trigger("rising"), .Select("low")) register_6 (
    .D(Data), .en(and_6_out), .Q(\行6 ), .clk(CLK), .clr(RST));
  Register #(.width(32), .trigger("rising"), .Select("low")) register_7 (
    .D(Data), .en(and_7_out), .Q(\行7 ), .clk(CLK), .clr(RST));
  Register #(.width(32), .trigger("rising"), .Select("low")) register_8 (
    .D(Data), .en(and_8_out), .Q(\行8 ), .clk(CLK), .clr(RST));
  and and_9 (and_9_out, En, \行9_t );
  and and_10 (and_10_out, En, \行10_t );
  and and_11 (and_11_out, En, \行11_t );
  and and_12 (and_12_out, En, \行12_t );
  and and_13 (and_13_out, En, \行13_t );
  and and_14 (and_14_out, En, \行14_t );
  and and_15 (and_15_out, En, \行15_t );
  and and_16 (and_16_out, En, \行16_t );
  Register #(.width(32), .trigger("rising"), .Select("low")) register_9 (
    .D(Data), .en(and_9_out), .Q(\行9 ), .clk(CLK), .clr(RST));
  Register #(.width(32), .trigger("rising"), .Select("low")) register_10 (
    .D(Data), .en(and_10_out), .Q(\行10 ), .clk(CLK), .clr(RST));
  Register #(.width(32), .trigger("rising"), .Select("low")) register_11 (
    .D(Data), .en(and_11_out), .Q(\行11 ), .clk(CLK), .clr(RST));
  Register #(.width(32), .trigger("rising"), .Select("low")) register_12 (
    .D(Data), .en(and_12_out), .Q(\行12 ), .clk(CLK), .clr(RST));
  Register #(.width(32), .trigger("rising"), .Select("low")) register_13 (
    .D(Data), .en(and_13_out), .Q(\行13 ), .clk(CLK), .clr(RST));
  Register #(.width(32), .trigger("rising"), .Select("low")) register_14 (
    .D(Data), .en(and_14_out), .Q(\行14 ), .clk(CLK), .clr(RST));
  Register #(.width(32), .trigger("rising"), .Select("low")) register_15 (
    .D(Data), .en(and_15_out), .Q(\行15 ), .clk(CLK), .clr(RST));
  Register #(.width(32), .trigger("rising"), .Select("low")) register_16 (
    .D(Data), .en(and_16_out), .Q(\行16 ), .clk(CLK), .clr(RST));
  and and_17 (and_17_out, En, \行17_t );
  and and_18 (and_18_out, En, \行18_t );
  and and_19 (and_19_out, En, \行19_t );
  and and_20 (and_20_out, En, \行20_t );
  and and_21 (and_21_out, En, \行21_t );
  and and_22 (and_22_out, En, \行22_t );
  and and_23 (and_23_out, En, \行23_t );
  and and_24 (and_24_out, En, \行24_t );
  Register #(.width(32), .trigger("rising"), .Select("low")) register_17 (
    .D(Data), .en(and_17_out), .Q(\行17 ), .clk(CLK), .clr(RST));
  Register #(.width(32), .trigger("rising"), .Select("low")) register_18 (
    .D(Data), .en(and_18_out), .Q(\行18 ), .clk(CLK), .clr(RST));
  Register #(.width(32), .trigger("rising"), .Select("low")) register_19 (
    .D(Data), .en(and_19_out), .Q(\行19 ), .clk(CLK), .clr(RST));
  Register #(.width(32), .trigger("rising"), .Select("low")) register_20 (
    .D(Data), .en(and_20_out), .Q(\行20 ), .clk(CLK), .clr(RST));
  Register #(.width(32), .trigger("rising"), .Select("low")) register_21 (
    .D(Data), .en(and_21_out), .Q(\行21 ), .clk(CLK), .clr(RST));
  Register #(.width(32), .trigger("rising"), .Select("low")) register_22 (
    .D(Data), .en(and_22_out), .Q(\行22 ), .clk(CLK), .clr(RST));
  Register #(.width(32), .trigger("rising"), .Select("low")) register_23 (
    .D(Data), .en(and_23_out), .Q(\行23 ), .clk(CLK), .clr(RST));
  Register #(.width(32), .trigger("rising"), .Select("low")) register_24 (
    .D(Data), .en(and_24_out), .Q(\行24 ), .clk(CLK), .clr(RST));
  and and_25 (and_25_out, En, \行25_t );
  and and_26 (and_26_out, En, \行26_t );
  and and_27 (and_27_out, En, \行27_t );
  and and_28 (and_28_out, En, \行28_t );
  and and_29 (and_29_out, En, \行29_t );
  and and_30 (and_30_out, En, \行30_t );
  and and_31 (and_31_out, En, \行31_t );
  and and_32 (and_32_out, En, \行32_t );
  Register #(.width(32), .trigger("rising"), .Select("low")) register_25 (
    .D(Data), .en(and_25_out), .Q(\行25 ), .clk(CLK), .clr(RST));
  Register #(.width(32), .trigger("rising"), .Select("low")) register_26 (
    .D(Data), .en(and_26_out), .Q(\行26 ), .clk(CLK), .clr(RST));
  Register #(.width(32), .trigger("rising"), .Select("low")) register_27 (
    .D(Data), .en(and_27_out), .Q(\行27 ), .clk(CLK), .clr(RST));
  Register #(.width(32), .trigger("rising"), .Select("low")) register_28 (
    .D(Data), .en(and_28_out), .Q(\行28 ), .clk(CLK), .clr(RST));
  Register #(.width(32), .trigger("rising"), .Select("low")) register_29 (
    .D(Data), .en(and_29_out), .Q(\行29 ), .clk(CLK), .clr(RST));
  Register #(.width(32), .trigger("rising"), .Select("low")) register_30 (
    .D(Data), .en(and_30_out), .Q(\行30 ), .clk(CLK), .clr(RST));
  Register #(.width(32), .trigger("rising"), .Select("low")) register_31 (
    .D(Data), .en(and_31_out), .Q(\行31 ), .clk(CLK), .clr(RST));
  Register #(.width(32), .trigger("rising"), .Select("low")) register_32 (
    .D(Data), .en(and_32_out), .Q(\行32 ), .clk(CLK), .clr(RST));
  Demultiplexer #(.select(5), .width(1), .tristate("false"), .disabled("Z"), .enable("false")) demultiplexer_1 (
    .out0(\行1_t ), .out1(\行2_t ), .out2(\行3_t ), .out3(\行4_t ), .out4(\行5_t ), .out5(\行6_t ), .out6(\行7_t ),
    .out7(\行8_t ), .out8(\行9_t ), .out9(\行10_t ), .out10(\行11_t ), .out11(\行12_t ), .out12(\行13_t ),
    .out13(\行14_t ), .out14(\行15_t ), .out15(\行16_t ), .out16(\行17_t ), .out17(\行18_t ), .out18(\行19_t ),
    .out19(\行20_t ), .out20(\行21_t ), .out21(\行22_t ), .out22(\行23_t ), .out23(\行24_t ), .out24(\行25_t ),
    .out25(\行26_t ), .out26(\行27_t ), .out27(\行28_t ), .out28(\行29_t ), .out29(\行30_t ), .out30(\行31_t ),
    .out31(\行32_t ), .in(1'b1), .sel(Addr[4:0]));
endmodule

module MapReg_2 (
  input  En,
  input  [31:0] _1,
  input  [31:0] _9,
  input  [31:0] _17,
  input  [31:0] _25,
  input  [31:0] _2,
  input  [31:0] _10,
  input  [31:0] _18,
  input  [31:0] _26,
  input  [31:0] _3,
  input  [31:0] _11,
  input  [31:0] _19,
  input  [31:0] _27,
  input  [31:0] _4,
  input  [31:0] _12,
  input  [31:0] _20,
  input  [31:0] _28,
  input  [31:0] _5,
  input  [31:0] _13,
  input  [31:0] _21,
  input  [31:0] _29,
  input  [31:0] _6,
  input  [31:0] _14,
  input  [31:0] _22,
  input  [31:0] _30,
  input  [31:0] _7,
  input  [31:0] _15,
  input  [31:0] _23,
  input  [31:0] _31,
  input  [31:0] _8,
  input  [31:0] _16,
  input  [31:0] _24,
  input  [31:0] _32,
  input  CLK,
  input  RST,
  output [31:0] \行1 ,
  output [31:0] \行9 ,
  output [31:0] \行17 ,
  output [31:0] \行25 ,
  output [31:0] \行2 ,
  output [31:0] \行10 ,
  output [31:0] \行18 ,
  output [31:0] \行26 ,
  output [31:0] \行3 ,
  output [31:0] \行11 ,
  output [31:0] \行19 ,
  output [31:0] \行27 ,
  output [31:0] \行4 ,
  output [31:0] \行12 ,
  output [31:0] \行20 ,
  output [31:0] \行28 ,
  output [31:0] \行5 ,
  output [31:0] \行13 ,
  output [31:0] \行21 ,
  output [31:0] \行29 ,
  output [31:0] \行6 ,
  output [31:0] \行14 ,
  output [31:0] \行22 ,
  output [31:0] \行30 ,
  output [31:0] \行7 ,
  output [31:0] \行15 ,
  output [31:0] \行23 ,
  output [31:0] \行31 ,
  output [31:0] \行8 ,
  output [31:0] \行16 ,
  output [31:0] \行24 ,
  output [31:0] \行32 
);

  Register #(.width(32), .trigger("rising"), .Select("low")) register_1 (
    .D(_1), .en(En), .Q(\行1 ), .clk(CLK), .clr(RST));
  Register #(.width(32), .trigger("rising"), .Select("low")) register_2 (
    .D(_2), .en(En), .Q(\行2 ), .clk(CLK), .clr(RST));
  Register #(.width(32), .trigger("rising"), .Select("low")) register_3 (
    .D(_3), .en(En), .Q(\行3 ), .clk(CLK), .clr(RST));
  Register #(.width(32), .trigger("rising"), .Select("low")) register_4 (
    .D(_4), .en(En), .Q(\行4 ), .clk(CLK), .clr(RST));
  Register #(.width(32), .trigger("rising"), .Select("low")) register_5 (
    .D(_5), .en(En), .Q(\行5 ), .clk(CLK), .clr(RST));
  Register #(.width(32), .trigger("rising"), .Select("low")) register_6 (
    .D(_6), .en(En), .Q(\行6 ), .clk(CLK), .clr(RST));
  Register #(.width(32), .trigger("rising"), .Select("low")) register_7 (
    .D(_7), .en(En), .Q(\行7 ), .clk(CLK), .clr(RST));
  Register #(.width(32), .trigger("rising"), .Select("low")) register_8 (
    .D(_8), .en(En), .Q(\行8 ), .clk(CLK), .clr(RST));
  Register #(.width(32), .trigger("rising"), .Select("low")) register_9 (
    .D(_9), .en(En), .Q(\行9 ), .clk(CLK), .clr(RST));
  Register #(.width(32), .trigger("rising"), .Select("low")) register_10 (
    .D(_10), .en(En), .Q(\行10 ), .clk(CLK), .clr(RST));
  Register #(.width(32), .trigger("rising"), .Select("low")) register_11 (
    .D(_11), .en(En), .Q(\行11 ), .clk(CLK), .clr(RST));
  Register #(.width(32), .trigger("rising"), .Select("low")) register_12 (
    .D(_12), .en(En), .Q(\行12 ), .clk(CLK), .clr(RST));
  Register #(.width(32), .trigger("rising"), .Select("low")) register_13 (
    .D(_13), .en(En), .Q(\行13 ), .clk(CLK), .clr(RST));
  Register #(.width(32), .trigger("rising"), .Select("low")) register_14 (
    .D(_14), .en(En), .Q(\行14 ), .clk(CLK), .clr(RST));
  Register #(.width(32), .trigger("rising"), .Select("low")) register_15 (
    .D(_15), .en(En), .Q(\行15 ), .clk(CLK), .clr(RST));
  Register #(.width(32), .trigger("rising"), .Select("low")) register_16 (
    .D(_16), .en(En), .Q(\行16 ), .clk(CLK), .clr(RST));
  Register #(.width(32), .trigger("rising"), .Select("low")) register_17 (
    .D(_17), .en(En), .Q(\行17 ), .clk(CLK), .clr(RST));
  Register #(.width(32), .trigger("rising"), .Select("low")) register_18 (
    .D(_18), .en(En), .Q(\行18 ), .clk(CLK), .clr(RST));
  Register #(.width(32), .trigger("rising"), .Select("low")) register_19 (
    .D(_19), .en(En), .Q(\行19 ), .clk(CLK), .clr(RST));
  Register #(.width(32), .trigger("rising"), .Select("low")) register_20 (
    .D(_20), .en(En), .Q(\行20 ), .clk(CLK), .clr(RST));
  Register #(.width(32), .trigger("rising"), .Select("low")) register_21 (
    .D(_21), .en(En), .Q(\行21 ), .clk(CLK), .clr(RST));
  Register #(.width(32), .trigger("rising"), .Select("low")) register_22 (
    .D(_22), .en(En), .Q(\行22 ), .clk(CLK), .clr(RST));
  Register #(.width(32), .trigger("rising"), .Select("low")) register_23 (
    .D(_23), .en(En), .Q(\行23 ), .clk(CLK), .clr(RST));
  Register #(.width(32), .trigger("rising"), .Select("low")) register_24 (
    .D(_24), .en(En), .Q(\行24 ), .clk(CLK), .clr(RST));
  Register #(.width(32), .trigger("rising"), .Select("low")) register_25 (
    .D(_25), .en(En), .Q(\行25 ), .clk(CLK), .clr(RST));
  Register #(.width(32), .trigger("rising"), .Select("low")) register_26 (
    .D(_26), .en(En), .Q(\行26 ), .clk(CLK), .clr(RST));
  Register #(.width(32), .trigger("rising"), .Select("low")) register_27 (
    .D(_27), .en(En), .Q(\行27 ), .clk(CLK), .clr(RST));
  Register #(.width(32), .trigger("rising"), .Select("low")) register_28 (
    .D(_28), .en(En), .Q(\行28 ), .clk(CLK), .clr(RST));
  Register #(.width(32), .trigger("rising"), .Select("low")) register_29 (
    .D(_29), .en(En), .Q(\行29 ), .clk(CLK), .clr(RST));
  Register #(.width(32), .trigger("rising"), .Select("low")) register_30 (
    .D(_30), .en(En), .Q(\行30 ), .clk(CLK), .clr(RST));
  Register #(.width(32), .trigger("rising"), .Select("low")) register_31 (
    .D(_31), .en(En), .Q(\行31 ), .clk(CLK), .clr(RST));
  Register #(.width(32), .trigger("rising"), .Select("low")) register_32 (
    .D(_32), .en(En), .Q(\行32 ), .clk(CLK), .clr(RST));
endmodule

module H_16_toD_10 (
  input  [7:0] Hex_16,
  output [3:0] \百位 ,
  output [3:0] \十位 ,
  output [3:0] \个位 
);

  wire [7:0] divider_1_out, divider_1_rem, divider_2_out, divider_2_rem;

  Divider #(.width(8)) divider_1 (.a(Hex_16), .b(8'ha), .out(divider_1_out), .rem(divider_1_rem));  // open: upper
  Divider #(.width(8)) divider_2 (
    .a(divider_1_out), .b(8'ha), .out(divider_2_out), .rem(divider_2_rem));  // open: upper
  Bit_Extender #(.in_width(8), .out_width(4), .\type ("zero")) bit_extender_1 (.in(divider_2_out), .out(\百位 ));
  Bit_Extender #(.in_width(8), .out_width(4), .\type ("zero")) bit_extender_2 (.in(divider_2_rem), .out(\十位 ));
  Bit_Extender #(.in_width(8), .out_width(4), .\type ("zero")) bit_extender_3 (.in(divider_1_rem), .out(\个位 ));
endmodule

module GameOver (
  input  [7:0] delHP,
  input  [7:0] exHP,
  output [3:0] \百位 ,
  output [3:0] \十位 ,
  output [3:0] \个位 ,
  output Gameover
);

  wire [7:0] subtractor_1_out;

  Subtractor #(.width(8)) subtractor_1 (.a(exHP), .b(delHP), .out(subtractor_1_out));  // open: bin, bout
  Comparator #(.width(8), .mode("twosComplement")) comparator_1 (.a(delHP), .b(exHP), .eq(Gameover));  // open: gt, lt
  H_16_toD_10 H_16_toD_10 (.Hex_16(subtractor_1_out), .\百位 (\百位 ), .\十位 (\十位 ), .\个位 (\个位 ));
endmodule

module \键盘操作电路  (
  input  [6:0] \键盘输入 ,
  input  CLK,
  input  RST,
  output LEFT_A,
  output RIGHT_D
);

  wire comparator_1_eq, comparator_2_eq;

  Comparator #(.width(7), .mode("twosComplement")) comparator_1 (
    .a(\键盘输入 ), .b(7'b1100001), .eq(comparator_1_eq));  // open: gt, lt
  Comparator #(.width(7), .mode("twosComplement")) comparator_2 (
    .a(\键盘输入 ), .b(7'b1100100), .eq(comparator_2_eq));  // open: gt, lt
  Register #(.width(1), .trigger("rising"), .Select("low")) register_1 (
    .D(comparator_1_eq), .Q(LEFT_A), .clk(CLK), .clr(RST));  // open: en
  Register #(.width(1), .trigger("rising"), .Select("low")) register_2 (
    .D(comparator_2_eq), .Q(RIGHT_D), .clk(CLK), .clr(RST));  // open: en
endmodule

module \频率控制电路  (
  input  [15:0] \延缓倍数 ,
  input  \原CLK ,
  input  RST,
  output \现CLK 
);

  wire comparator_1_eq, comparator_2_eq, comparator_2_gt, or_1_out;
  wire [15:0] counter_1_q, shifter_1_out;

  Counter #(.width(16), .max('hffff), .ongoal("wrap"), .trigger("rising"), .behavior("new")) counter_1 (
    .load(comparator_1_eq), .D({16{1'b0}}), .Q(counter_1_q), .clk(\原CLK ), .clr(RST));  // open: count, carry, preset, down
  Shifter #(.width(16), .shift("lr")) shifter_1 (.in(\延缓倍数 ), .\dist (4'b0001), .out(shifter_1_out));
  Comparator #(.width(16), .mode("twosComplement")) comparator_1 (
    .a(\延缓倍数 ), .b(counter_1_q), .eq(comparator_1_eq));  // open: gt, lt
  Comparator #(.width(16), .mode("twosComplement")) comparator_2 (
    .a(shifter_1_out), .b(counter_1_q), .gt(comparator_2_gt), .eq(comparator_2_eq));  // open: lt
  or or_1 (or_1_out, comparator_2_gt, comparator_2_eq);
  Multiplexer #(.select(1), .width(1), .disabled("Z"), .enable("false")) multiplexer_1 (
    .in0(1'b1), .in1(1'b0), .out(\现CLK ), .sel(or_1_out));
endmodule
